// Logisim project 4bit_swap.circ as structural Verilog: 5 circuits, main circuit main
module main (
);

  _4bit_sort u_4bit_sort_1 ();  // open: in_1, in_2, in_3, in_4, out_5, out_6, out_7, out_8
endmodule

module _1bit_swap (
  input  in_1,
  input  in_2,
  input  in_3,
  output out_4,
  output out_5
);

  wire not_1_out;

  assign out_4 = not_1_out ? in_1 : 1'bz;  // Controlled_Buffer controlled_buffer_1
  not not_1 (not_1_out, in_3);
  assign out_5 = in_3 ? in_1 : 1'bz;  // Controlled_Buffer controlled_buffer_2
  assign out_5 = not_1_out ? in_2 : 1'bz;  // Controlled_Buffer controlled_buffer_3
  assign out_4 = in_3 ? in_2 : 1'bz;  // Controlled_Buffer controlled_buffer_4
endmodule

module _4bit_swap (
  input  [3:0] in_1,
  input  [3:0] in_2,
  input  in_3,
  output [3:0] out_4,
  output [3:0] out_5
);

  wire not_1_out;

  assign out_4 = not_1_out ? in_1 : 4'bz;  // Controlled_Buffer controlled_buffer_1
  assign out_5 = in_3 ? in_1 : 4'bz;  // Controlled_Buffer controlled_buffer_2
  not not_1 (not_1_out, in_3);
  assign out_4 = in_3 ? in_2 : 4'bz;  // Controlled_Buffer controlled_buffer_3
  assign out_5 = not_1_out ? in_2 : 4'bz;  // Controlled_Buffer controlled_buffer_4
endmodule

module _4bit_sort (
  input  [3:0] in_1,
  input  [3:0] in_2,
  input  [3:0] in_3,
  input  [3:0] in_4,
  output [3:0] out_5,
  output [3:0] out_6,
  output [3:0] out_7,
  output [3:0] out_8
);

  wire comparator_1_eq, comparator_1_gt, comparator_2_gt, comparator_3_gt, comparator_4_gt, comparator_5_gt,
       comparator_6_gt;
  wire [3:0] n4bit_swap_1_out_4, n4bit_swap_1_out_5, n4bit_swap_2_out_4, n4bit_swap_2_out_5,
       n4bit_swap_3_out_5, n4bit_swap_4_out_4, n4bit_swap_4_out_5, n4bit_swap_5_out_5;

  _4bit_swap u_4bit_swap_1 (
    .in_1(in_1), .in_2(in_2), .in_3(comparator_1_gt), .out_4(n4bit_swap_1_out_4), .out_5(n4bit_swap_1_out_5));
  Comparator #(.width(4), .mode("unsigned")) comparator_1 (
    .a(in_1), .b(in_2), .gt(comparator_1_gt), .eq(comparator_1_eq), .lt(comparator_1_eq));
  Comparator #(.width(4), .mode("unsigned")) comparator_2 (
    .a(n4bit_swap_1_out_4), .b(in_3), .gt(comparator_2_gt));  // open: eq, lt
  _4bit_swap u_4bit_swap_2 (
    .in_1(n4bit_swap_1_out_4), .in_2(in_3), .in_3(comparator_2_gt), .out_4(n4bit_swap_2_out_4),
    .out_5(n4bit_swap_2_out_5));
  _4bit_swap u_4bit_swap_3 (
    .in_1(n4bit_swap_2_out_4), .in_2(in_4), .in_3(comparator_3_gt), .out_4(out_5), .out_5(n4bit_swap_3_out_5));
  Comparator #(.width(4), .mode("unsigned")) comparator_3 (
    .a(n4bit_swap_2_out_4), .b(in_4), .gt(comparator_3_gt));  // open: eq, lt
  _4bit_swap u_4bit_swap_4 (
    .in_1(n4bit_swap_1_out_5), .in_2(n4bit_swap_2_out_5), .in_3(comparator_4_gt), .out_4(n4bit_swap_4_out_4),
    .out_5(n4bit_swap_4_out_5));
  Comparator #(.width(4), .mode("unsigned")) comparator_4 (
    .a(n4bit_swap_1_out_5), .b(n4bit_swap_2_out_5), .gt(comparator_4_gt));  // open: eq, lt
  Comparator #(.width(4), .mode("unsigned")) comparator_5 (
    .a(n4bit_swap_4_out_4), .b(n4bit_swap_3_out_5), .gt(comparator_5_gt));  // open: eq, lt
  _4bit_swap u_4bit_swap_5 (
    .in_1(n4bit_swap_4_out_4), .in_2(n4bit_swap_3_out_5), .in_3(comparator_5_gt), .out_4(out_6),
    .out_5(n4bit_swap_5_out_5));
  _4bit_swap u_4bit_swap_6 (
    .in_1(n4bit_swap_4_out_5), .in_2(n4bit_swap_5_out_5), .in_3(comparator_6_gt), .out_4(out_7), .out_5(out_8));
  Comparator #(.width(4), .mode("unsigned")) comparator_6 (
    .a(n4bit_swap_4_out_5), .b(n4bit_swap_5_out_5), .gt(comparator_6_gt));  // open: eq, lt
endmodule

module test (
  input  [3:0] in_1,
  input  [3:0] in_2
);

  wire comparator_1_eq, comparator_1_gt, comparator_1_lt;

  Comparator #(.width(4)) comparator_1 (
    .a(in_1), .b(in_2), .gt(comparator_1_gt), .eq(comparator_1_eq), .lt(comparator_1_lt));
endmodule
