// Logisim project CRC.circ as structural Verilog: 2 circuits, main circuit main
module main (
  input  [3:0] BEI,
  input  [3:0] CHU,
  output [2:0] out_3
);

  wire xor_1_out, xor_2_out, xor_3_out;

  xor xor_1 (xor_1_out, BEI[0], CHU[0]);
  xor xor_2 (xor_2_out, BEI[1], CHU[1]);
  xor xor_3 (xor_3_out, BEI[2], CHU[2]);
  Multiplexer #(.enable("false")) multiplexer_1 (.in0(BEI[0]), .in1(xor_1_out), .out(out_3[0]), .sel(BEI[3]));
  Multiplexer #(.enable("false")) multiplexer_2 (.in0(BEI[1]), .in1(xor_2_out), .out(out_3[1]), .sel(BEI[3]));
  Multiplexer #(.enable("false")) multiplexer_3 (.in0(BEI[2]), .in1(xor_3_out), .out(out_3[2]), .sel(BEI[3]));
endmodule

module CRC (
  input  [7:0] in_1,
  input  [3:0] in_2,
  output [10:0] out_3
);

  wire [2:0] main_1_out_3, main_2_out_3, main_3_out_3, main_4_out_3, main_5_out_3, main_6_out_3, main_7_out_3;

  main main_1 (.BEI({in_1[4], in_1[5], in_1[6], in_1[7]}), .CHU(in_2), .out_3(main_1_out_3));
  main main_2 (.BEI({main_1_out_3, in_1[3]}), .CHU(in_2), .out_3(main_2_out_3));
  main main_3 (.BEI({main_2_out_3, in_1[2]}), .CHU(in_2), .out_3(main_3_out_3));
  main main_4 (.BEI({main_3_out_3, in_1[1]}), .CHU(in_2), .out_3(main_4_out_3));
  main main_5 (.BEI({main_4_out_3, in_1[0]}), .CHU(in_2), .out_3(main_5_out_3));
  main main_6 (.BEI({main_5_out_3, 1'b0}), .CHU(in_2), .out_3(main_6_out_3));
  main main_7 (.BEI({main_6_out_3, 1'b0}), .CHU(in_2), .out_3(main_7_out_3));
  main main_8 (.BEI({main_7_out_3, 1'b0}), .CHU(in_2), .out_3(out_3[2:0]));
  // Probe on out_3[2:0]

  assign out_3[10:3] = in_1;

  // Other names for the same wires on the sheet: go[3:0] = in_2
endmodule
