// Logisim project Single_Cycle_MicroA.circ as structural Verilog: 12 circuits, main circuit main
module main (
  input  Reset,
  output [31:0] out_2,
  output out_3,
  output [4:0] out_4,
  output [31:0] out_5,
  output out_6,
  output [4:0] out_7,
  output [31:0] out_8
);

  wire alu_1_zero, ALUSrc, and_1_out, bne, Branch, byte_op, clock_1_out, Ext_Op, j_Op, jr, luiOp, MemtoReg,
       multiplexer_6_out, not_1_out, or_1_out, RegDst;
  wire [2:0] ALUControl;
  wire [4:0] multiplexer_5_out;
  wire [31:0] dm_1_out_6, ext_1_out_3, grf_1_out_9, ifu_1_instr_2, MemAddr, multiplexer_1_out,
       multiplexer_2_out, multiplexer_4_out;

  // Probe on out_2
  Clock clock_1 (.out(clock_1_out));
  or or_1 (or_1_out, j_Op, jr);
  IFU ifu_1 (
    .Instr(out_2), .in_3(multiplexer_2_out), .PCSrc(and_1_out), .Reset(Reset), .clk(clock_1_out),
    .in_1(or_1_out), .Instr_2(ifu_1_instr_2));
  Multiplexer #(.width(32), .enable("false")) multiplexer_1 (
    .in0(ext_1_out_3), .in1({{6{1'b0}}, out_2[25:0]}), .out(multiplexer_1_out), .sel(j_Op));
  Multiplexer #(.width(32), .enable("false")) multiplexer_2 (
    .in0(multiplexer_1_out), .in1(grf_1_out_9), .out(multiplexer_2_out), .sel(jr));
  Multiplexer #(.width(5), .enable("false")) multiplexer_3 (
    .in0(out_2[20:16]), .in1(out_2[15:11]), .out(out_4), .sel(RegDst));
  CU cu_1 (
    .Opcode(out_2[31:26]), .Funct(out_2[5:0]), .out_14(ALUControl), .MemtoReg(MemtoReg), .MemWrite(out_6),
    .Branch(Branch), .ALUSrc(ALUSrc), .RegDst(RegDst), .RegWrite(out_3), .j_Op(j_Op), .luiOp(luiOp),
    .byte_Op(byte_op), .Ext_Op(Ext_Op), .bne(bne), .jr(jr));
  // Probe on ALUControl
  GRF grf_1 (
    ._21_25(out_2[25:21]), ._16_20(out_2[20:16]), .Addr(out_4), .Addr_2(out_5), .out_9(grf_1_out_9),
    .out_10(out_8), .in_6(clock_1_out), .in_1(out_3), .PC_4(ifu_1_instr_2), .jal(j_Op));
  Ext ext_1 (.in_2(out_2[15:0]), .out_3(ext_1_out_3), .Ext_op(Ext_Op));
  Multiplexer #(.width(32), .enable("false")) multiplexer_4 (
    .in0(out_8), .in1(ext_1_out_3), .out(multiplexer_4_out), .sel(ALUSrc));
  Multiplexer #(.width(5), .enable("false")) multiplexer_5 (
    .in0(out_2[10:6]), .in1(5'b10000), .out(multiplexer_5_out), .sel(luiOp));
  Multiplexer #(.enable("false")) multiplexer_6 (.in0(alu_1_zero), .in1(not_1_out), .out(multiplexer_6_out), .sel(bne));
  not not_1 (not_1_out, alu_1_zero);
  ALU alu_1 (
    .Src0(grf_1_out_9), .Src1(multiplexer_4_out), .zero(alu_1_zero), .in_1(ALUControl),
    .shamt(multiplexer_5_out), .out_6({MemAddr[31:7], out_7, MemAddr[1:0]}));
  and and_1 (and_1_out, Branch, multiplexer_6_out);
  Multiplexer #(.width(32), .enable("false")) multiplexer_7 (
    .in0({MemAddr[31:7], out_7, MemAddr[1:0]}), .in1(dm_1_out_6), .out(out_5), .sel(MemtoReg));
  DM dm_1 (
    .Addr({MemAddr[31:7], out_7, MemAddr[1:0]}), .Data(out_8), .out_6(dm_1_out_6), .byte_Op(byte_op),
    .MemWrite(out_6), .Clk(clock_1_out));

  // Other names for the same wires on the sheet: Instr[31:0] = out_2; Funct[5:0] = out_2[5:0];
  //   Opcode[5:0] = out_2[31:26]; MemAddr[6:2] = out_7; Memdata[31:0] = out_8; MemWrite = out_6; RegAddr[4:0] = out_4;
  //   RegDATA[31:0] = out_5; RegWrite = out_3
endmodule

module GRF (
  input  in_1,
  input  [4:0] _21_25,
  input  [4:0] _16_20,
  input  [4:0] Addr,
  input  [31:0] Addr_2,
  input  in_6,
  input  [31:0] PC_4,
  input  jal,
  output [31:0] out_9,
  output [31:0] out_10
);

  wire and_1_out, and_in_grf_1_out_3, and_in_grf_1_out_4, and_in_grf_1_out_5, and_in_grf_1_out_6,
       and_in_grf_2_out_3, and_in_grf_2_out_4, and_in_grf_2_out_5, and_in_grf_2_out_6, and_in_grf_3_out_3,
       and_in_grf_3_out_4, and_in_grf_3_out_5, and_in_grf_3_out_6, and_in_grf_4_out_3, and_in_grf_4_out_4,
       and_in_grf_4_out_5, and_in_grf_4_out_6, and_in_grf_5_out_3, and_in_grf_5_out_4, and_in_grf_5_out_5,
       and_in_grf_5_out_6, and_in_grf_6_out_3, and_in_grf_6_out_4, and_in_grf_6_out_5, and_in_grf_6_out_6,
       and_in_grf_7_out_3, and_in_grf_7_out_4, and_in_grf_7_out_5, and_in_grf_7_out_6, and_in_grf_8_out_3,
       and_in_grf_8_out_4, and_in_grf_8_out_5, and_in_grf_8_out_6, or_1_out;
  wire [3:0] decoder_1_out0, decoder_1_out4, decoder_1_out8, decoder_1_out12, decoder_1_out16,
       decoder_1_out20, decoder_1_out24, decoder_1_out28;
  wire [31:0] _0_q, a0_q, a1_q, a2_q, a3_q, at_q, fp_q, gp_q, k0_q, k1_q, ra, ra_q, s0_q, s1_q, s2_q, s3_q,
       s4_q, s5_q, s6_q, s7_q, sp_q, t0_q, t1_q, t2_q, t3_q, t4_q, t5_q, t6_q, t7_q, t8_q, t9_q, v0_q, v1_q;

  Decoder #(.select(5), .enable("false")) decoder_1 (
    .out0(decoder_1_out0[0]), .out1(decoder_1_out0[1]), .out2(decoder_1_out0[2]), .out3(decoder_1_out0[3]),
    .out4(decoder_1_out4[0]), .out5(decoder_1_out4[1]), .out6(decoder_1_out4[2]), .out7(decoder_1_out4[3]),
    .out8(decoder_1_out8[0]), .out9(decoder_1_out8[1]), .out10(decoder_1_out8[2]), .out11(decoder_1_out8[3]),
    .out12(decoder_1_out12[0]), .out13(decoder_1_out12[1]), .out14(decoder_1_out12[2]),
    .out15(decoder_1_out12[3]), .out16(decoder_1_out16[0]), .out17(decoder_1_out16[1]),
    .out18(decoder_1_out16[2]), .out19(decoder_1_out16[3]), .out20(decoder_1_out20[0]),
    .out21(decoder_1_out20[1]), .out22(decoder_1_out20[2]), .out23(decoder_1_out20[3]),
    .out24(decoder_1_out24[0]), .out25(decoder_1_out24[1]), .out26(decoder_1_out24[2]),
    .out27(decoder_1_out24[3]), .out28(decoder_1_out28[0]), .out29(decoder_1_out28[1]),
    .out30(decoder_1_out28[2]), .out31(decoder_1_out28[3]), .sel(Addr));
  AND_in_GRF and_in_grf_1 (
    .in_1(decoder_1_out0), .in_2(in_1), .out_3(and_in_grf_1_out_3), .out_4(and_in_grf_1_out_4),
    .out_5(and_in_grf_1_out_5), .out_6(and_in_grf_1_out_6));
  AND_in_GRF and_in_grf_2 (
    .in_1(decoder_1_out4), .in_2(in_1), .out_3(and_in_grf_2_out_3), .out_4(and_in_grf_2_out_4),
    .out_5(and_in_grf_2_out_5), .out_6(and_in_grf_2_out_6));
  AND_in_GRF and_in_grf_3 (
    .in_1(decoder_1_out8), .in_2(in_1), .out_3(and_in_grf_3_out_3), .out_4(and_in_grf_3_out_4),
    .out_5(and_in_grf_3_out_5), .out_6(and_in_grf_3_out_6));
  AND_in_GRF and_in_grf_4 (
    .in_1(decoder_1_out12), .in_2(in_1), .out_3(and_in_grf_4_out_3), .out_4(and_in_grf_4_out_4),
    .out_5(and_in_grf_4_out_5), .out_6(and_in_grf_4_out_6));
  AND_in_GRF and_in_grf_5 (
    .in_1(decoder_1_out16), .in_2(in_1), .out_3(and_in_grf_5_out_3), .out_4(and_in_grf_5_out_4),
    .out_5(and_in_grf_5_out_5), .out_6(and_in_grf_5_out_6));
  AND_in_GRF and_in_grf_6 (
    .in_1(decoder_1_out20), .in_2(in_1), .out_3(and_in_grf_6_out_3), .out_4(and_in_grf_6_out_4),
    .out_5(and_in_grf_6_out_5), .out_6(and_in_grf_6_out_6));
  AND_in_GRF and_in_grf_7 (
    .in_1(decoder_1_out24), .in_2(in_1), .out_3(and_in_grf_7_out_3), .out_4(and_in_grf_7_out_4),
    .out_5(and_in_grf_7_out_5), .out_6(and_in_grf_7_out_6));
  AND_in_GRF and_in_grf_8 (
    .in_1(decoder_1_out28), .in_2(in_1), .out_3(and_in_grf_8_out_3), .out_4(and_in_grf_8_out_4),
    .out_5(and_in_grf_8_out_5), .out_6(and_in_grf_8_out_6));
  Multiplexer #(.width(32), .enable("false")) multiplexer_1 (.in0(Addr_2), .in1(PC_4), .out(ra), .sel(jal));
  Register #(.width(32)) _0 (.D(Addr_2), .en(1'b0), .Q(_0_q), .clk(in_6));  // open: clr
  Register #(.width(32)) a0 (.D(Addr_2), .en(and_in_grf_2_out_3), .Q(a0_q), .clk(in_6));  // open: clr
  Register #(.width(32)) t0 (.D(Addr_2), .en(and_in_grf_3_out_3), .Q(t0_q), .clk(in_6));  // open: clr
  Register #(.width(32)) t4 (.D(Addr_2), .en(and_in_grf_4_out_3), .Q(t4_q), .clk(in_6));  // open: clr
  Register #(.width(32)) s0 (.D(Addr_2), .en(and_in_grf_5_out_3), .Q(s0_q), .clk(in_6));  // open: clr
  Register #(.width(32)) s4 (.D(Addr_2), .en(and_in_grf_6_out_3), .Q(s4_q), .clk(in_6));  // open: clr
  Register #(.width(32)) t8 (.D(Addr_2), .en(and_in_grf_7_out_3), .Q(t8_q), .clk(in_6));  // open: clr
  Register #(.width(32)) gp (.D(Addr_2), .en(and_in_grf_8_out_3), .Q(gp_q), .clk(in_6));  // open: clr
  and and_1 (and_1_out, in_1, jal);
  Register #(.width(32)) at (.D(Addr_2), .en(and_in_grf_1_out_4), .Q(at_q), .clk(in_6));  // open: clr
  Register #(.width(32)) a1 (.D(Addr_2), .en(and_in_grf_2_out_4), .Q(a1_q), .clk(in_6));  // open: clr
  Register #(.width(32)) t1 (.D(Addr_2), .en(and_in_grf_3_out_4), .Q(t1_q), .clk(in_6));  // open: clr
  Register #(.width(32)) t5 (.D(Addr_2), .en(and_in_grf_4_out_4), .Q(t5_q), .clk(in_6));  // open: clr
  Register #(.width(32)) s1 (.D(Addr_2), .en(and_in_grf_5_out_4), .Q(s1_q), .clk(in_6));  // open: clr
  Register #(.width(32)) s5 (.D(Addr_2), .en(and_in_grf_6_out_4), .Q(s5_q), .clk(in_6));  // open: clr
  Register #(.width(32)) t9 (.D(Addr_2), .en(and_in_grf_7_out_4), .Q(t9_q), .clk(in_6));  // open: clr
  Register #(.width(32)) sp (.D(Addr_2), .en(and_in_grf_8_out_4), .Q(sp_q), .clk(in_6));  // open: clr
  Register #(.width(32)) v0 (.D(Addr_2), .en(and_in_grf_1_out_5), .Q(v0_q), .clk(in_6));  // open: clr
  Register #(.width(32)) a2 (.D(Addr_2), .en(and_in_grf_2_out_5), .Q(a2_q), .clk(in_6));  // open: clr
  Register #(.width(32)) t2 (.D(Addr_2), .en(and_in_grf_3_out_5), .Q(t2_q), .clk(in_6));  // open: clr
  Register #(.width(32)) t6 (.D(Addr_2), .en(and_in_grf_4_out_5), .Q(t6_q), .clk(in_6));  // open: clr
  Register #(.width(32)) s2 (.D(Addr_2), .en(and_in_grf_5_out_5), .Q(s2_q), .clk(in_6));  // open: clr
  Register #(.width(32)) s6 (.D(Addr_2), .en(and_in_grf_6_out_5), .Q(s6_q), .clk(in_6));  // open: clr
  Register #(.width(32)) k0 (.D(Addr_2), .en(and_in_grf_7_out_5), .Q(k0_q), .clk(in_6));  // open: clr
  Register #(.width(32)) fp (.D(Addr_2), .en(and_in_grf_8_out_5), .Q(fp_q), .clk(in_6));  // open: clr
  or or_1 (or_1_out, and_1_out, and_in_grf_8_out_6);
  Register #(.width(32)) v1 (.D(Addr_2), .en(and_in_grf_1_out_6), .Q(v1_q), .clk(in_6));  // open: clr
  Register #(.width(32)) a3 (.D(Addr_2), .en(and_in_grf_2_out_6), .Q(a3_q), .clk(in_6));  // open: clr
  Register #(.width(32)) t3 (.D(Addr_2), .en(and_in_grf_3_out_6), .Q(t3_q), .clk(in_6));  // open: clr
  Register #(.width(32)) t7 (.D(Addr_2), .en(and_in_grf_4_out_6), .Q(t7_q), .clk(in_6));  // open: clr
  Register #(.width(32)) s3 (.D(Addr_2), .en(and_in_grf_5_out_6), .Q(s3_q), .clk(in_6));  // open: clr
  Register #(.width(32)) s7 (.D(Addr_2), .en(and_in_grf_6_out_6), .Q(s7_q), .clk(in_6));  // open: clr
  Register #(.width(32)) k1 (.D(Addr_2), .en(and_in_grf_7_out_6), .Q(k1_q), .clk(in_6));  // open: clr
  Register #(.width(32)) u_ra (.D(ra), .en(or_1_out), .Q(ra_q), .clk(in_6));  // open: clr
  Multiplexer #(.select(5), .width(32), .enable("false")) multiplexer_2 (
    .in0(_0_q), .in1(at_q), .in2(v0_q), .in3(v1_q), .in4(a0_q), .in5(a1_q), .in6(a2_q), .in7(a3_q),
    .in8(t0_q), .in9(t1_q), .in10(t2_q), .in11(t3_q), .in12(t4_q), .in13(t5_q), .in14(t6_q), .in15(t7_q),
    .in16(s0_q), .in17(s1_q), .in18(s2_q), .in19(s3_q), .in20(s4_q), .in21(s5_q), .in22(s6_q), .in23(s7_q),
    .in24(t8_q), .in25(t9_q), .in26(k0_q), .in27(k1_q), .in28(gp_q), .in29(sp_q), .in30(fp_q), .in31(ra_q),
    .out(out_9), .sel(_21_25));
  Multiplexer #(.select(5), .width(32), .enable("false")) multiplexer_3 (
    .in0(_0_q), .in1(at_q), .in2(v0_q), .in3(v1_q), .in4(a0_q), .in5(a1_q), .in6(a2_q), .in7(a3_q),
    .in8(t0_q), .in9(t1_q), .in10(t2_q), .in11(t3_q), .in12(t4_q), .in13(t5_q), .in14(t6_q), .in15(t7_q),
    .in16(s0_q), .in17(s1_q), .in18(s2_q), .in19(s3_q), .in20(s4_q), .in21(s5_q), .in22(s6_q), .in23(s7_q),
    .in24(t8_q), .in25(t9_q), .in26(k0_q), .in27(k1_q), .in28(gp_q), .in29(sp_q), .in30(fp_q), .in31(ra_q),
    .out(out_10), .sel(_16_20));

  // Other names for the same wires on the sheet: DATA[31:0] = Addr_2; RD1[4:0] = _21_25; RD2[4:0] = _16_20
endmodule

module AND_in_GRF (
  input  [3:0] in_1,
  input  in_2,
  output out_3,
  output out_4,
  output out_5,
  output out_6
);

  and and_1 (out_3, in_1[0], in_2);
  and and_2 (out_4, in_1[1], in_2);
  and and_3 (out_5, in_1[2], in_2);
  and and_4 (out_6, in_1[3], in_2);
endmodule

module ALU (
  input  [2:0] in_1,
  input  [31:0] Src0,
  input  [31:0] Src1,
  input  [4:0] shamt,
  output zero,
  output [31:0] out_6
);

  wire [0:0] comparator_1_lt;
  wire [31:0] adder_1_out, and_1_out, or_1_out, shifter_1_out, subtractor_1_out;

  Adder #(.width(32)) adder_1 (.a(Src0), .b(Src1), .out(adder_1_out));  // open: cin, cout
  Subtractor #(.width(32)) subtractor_1 (.a(Src0), .b(Src1), .out(subtractor_1_out));  // open: bin, bout
  assign and_1_out = Src0 & Src1;  // AND_Gate and_1, 32 bits wide
  assign or_1_out = Src0 | Src1;  // OR_Gate or_1, 32 bits wide
  Comparator #(.width(32)) comparator_1 (.a(Src0), .b(Src1), .lt(comparator_1_lt[0]));  // open: gt, eq
  Shifter #(.width(32)) shifter_1 (.in(Src1), .\dist (shamt), .out(shifter_1_out));
  Multiplexer #(.select(3), .width(32), .enable("false")) multiplexer_1 (
    .in0(adder_1_out), .in1(subtractor_1_out), .in2(and_1_out), .in3(or_1_out),
    .in4({{31{1'b0}}, comparator_1_lt[0]}), .in5(shifter_1_out), .out(out_6), .sel(in_1));  // open: in6, in7
  Comparator #(.width(32), .mode("unsigned")) comparator_2 (
    .a({32{1'b0}}), .b(subtractor_1_out), .eq(zero));  // open: gt, lt
endmodule

module DM (
  input  byte_Op,
  input  [31:0] Addr,
  input  [31:0] Data,
  input  MemWrite,
  input  Clk,
  output [31:0] out_6
);

  wire [4:0] multiplier_1_out, multiplier_2_out;
  wire [31:0] adder_1_out, multiplexer_1_out, ram_1_data, shifter_1_out, shifter_2_out;

  Shifter #(.width(32)) shifter_1 (.in(Data), .\dist (multiplier_1_out), .out(shifter_1_out));
  Multiplier #(.width(5)) multiplier_1 (
    .a({3'b000, Addr[1:0]}), .b(5'b00010), .out(multiplier_1_out));  // open: cin, cout
  Adder #(.width(32)) adder_1 (.a(shifter_1_out), .b(ram_1_data), .out(adder_1_out));  // open: cin, cout
  Multiplexer #(.width(32), .enable("false")) multiplexer_1 (
    .in0(Data), .in1(adder_1_out), .out(multiplexer_1_out), .sel(byte_Op));
  RAM #(.addrWidth(5), .dataWidth(32), .bus("separate")) ram_1 (
    .addr(Addr[6:2]), .din(multiplexer_1_out), .data(ram_1_data), .str(MemWrite), .clk(Clk));  // open: sel, ld, clr
  Multiplier #(.width(5)) multiplier_2 (
    .a({3'b000, Addr[1:0]}), .b(5'b00010), .out(multiplier_2_out));  // open: cin, cout
  Shifter #(.width(32), .shift("lr")) shifter_2 (.in(ram_1_data), .\dist (multiplier_2_out), .out(shifter_2_out));
  Multiplexer #(.width(32), .enable("false")) multiplexer_2 (
    .in0(ram_1_data), .in1(shifter_2_out), .out(out_6), .sel(byte_Op));

  // Other names for the same wires on the sheet: byte[1:0] = Addr[1:0]
endmodule

// Control
module CU (
  input  [5:0] Opcode,
  input  [5:0] Funct,
  output MemtoReg,
  output MemWrite,
  output Branch,
  output ALUSrc,
  output RegDst,
  output RegWrite,
  output j_Op,
  output luiOp,
  output byte_Op,
  output Ext_Op,
  output bne,
  output [2:0] out_14,
  output jr
);

  wire control_op_decode_1_addi, control_op_decode_1_addiu, control_op_decode_1_beq, control_op_decode_1_bne,
       control_op_decode_1_j, control_op_decode_1_jal, control_op_decode_1_lb, control_op_decode_1_lui,
       control_op_decode_1_lw, control_op_decode_1_ori, control_op_decode_1_r, control_op_decode_1_sb,
       control_op_decode_1_sw, cu_funct_alu_1_jr, Pri;
  wire [2:0] cu_funct_alu_1_aluc0, cu_opcode_alu_1_aluc0;

  CU_Opcode_ALU cu_opcode_alu_1 (
    .o5(Opcode[5]), .o4(Opcode[4]), .o3(Opcode[3]), .o2(Opcode[2]), .o1(Opcode[1]), .o0(Opcode[0]),
    .ALUC2(cu_opcode_alu_1_aluc0[2]), .ALUC1(cu_opcode_alu_1_aluc0[1]), .ALUC0(cu_opcode_alu_1_aluc0[0]));
  CU_Funct_Alu cu_funct_alu_1 (
    .i5(Funct[5]), .i4(Funct[4]), .i3(Funct[3]), .i2(Funct[2]), .i1(Funct[1]), .i0(Funct[0]),
    .ALUC2(cu_funct_alu_1_aluc0[2]), .ALUC1(cu_funct_alu_1_aluc0[1]), .ALUC0(cu_funct_alu_1_aluc0[0]),
    .jr(cu_funct_alu_1_jr));
  or or_1 (Pri, Opcode[0], Opcode[1], Opcode[2], Opcode[3], Opcode[4], Opcode[5]);
  Multiplexer #(.width(3), .enable("false")) multiplexer_1 (
    .in0(cu_funct_alu_1_aluc0), .in1(cu_opcode_alu_1_aluc0), .out(out_14), .sel(Pri));
  and and_1 (jr, cu_funct_alu_1_jr, ~Pri);  // AND_Gate
  Control_op_decode control_op_decode_1 (
    ._5(Opcode[5]), ._4(Opcode[4]), ._3(Opcode[3]), ._2(Opcode[2]), ._1(Opcode[1]), ._0(Opcode[0]),
    .R(control_op_decode_1_r), .ori(control_op_decode_1_ori), .beq(control_op_decode_1_beq),
    .bne(control_op_decode_1_bne), .sw(control_op_decode_1_sw), .lw(control_op_decode_1_lw),
    .lui(control_op_decode_1_lui), .j(control_op_decode_1_j), .jal(control_op_decode_1_jal),
    .sb(control_op_decode_1_sb), .lb(control_op_decode_1_lb), .addi(control_op_decode_1_addi),
    .addiu(control_op_decode_1_addiu));
  Control_or_logic control_or_logic_1 (
    .R(control_op_decode_1_r), .ori(control_op_decode_1_ori), .beq(control_op_decode_1_beq),
    .bne(control_op_decode_1_bne), .sw(control_op_decode_1_sw), .lw(control_op_decode_1_lw),
    .lui(control_op_decode_1_lui), .j(control_op_decode_1_j), .jal(control_op_decode_1_jal),
    .sb(control_op_decode_1_sb), .lb(control_op_decode_1_lb), .addi(control_op_decode_1_addi),
    .addiu(control_op_decode_1_addiu), .MemtoReg(MemtoReg), .MemWrite(MemWrite), .Branch(Branch),
    .ALUSrc(ALUSrc), .RegDst(RegDst), .RegWrite(RegWrite), .j_Op(j_Op), .luiOp(luiOp), .byte_Op(byte_Op),
    .Ext_Op(Ext_Op), .bne_2(bne));  // open: in_14, in_15
endmodule

module CU_Funct_Alu (
  input  i5,
  input  i4,
  input  i3,
  input  i2,
  input  i1,
  input  i0,
  output ALUC2,
  output ALUC1,
  output ALUC0,
  output jr
);

  wire and_2_out, and_3_out, and_4_out, and_5_out, and_6_out, and_7_out, and_8_out, and_9_out, and_10_out,
       and_11_out, not_1_out, not_2_out, not_3_out, not_4_out, not_5_out, not_6_out, not_7_out, not_8_out,
       not_9_out, not_10_out, not_11_out, not_12_out, not_13_out, not_14_out, not_15_out, not_16_out,
       not_17_out, not_18_out, not_19_out, not_20_out;

  not not_1 (not_1_out, i5);
  not not_2 (not_2_out, i4);
  not not_3 (not_3_out, i3);
  not not_4 (not_4_out, i2);
  not not_5 (not_5_out, i1);
  not not_6 (not_6_out, i0);
  not not_7 (not_7_out, i4);
  not not_8 (not_8_out, i2);
  not not_9 (not_9_out, i0);
  and and_1 (ALUC1, i5, i2);
  not not_10 (not_10_out, i5);
  not not_11 (not_11_out, i4);
  not not_12 (not_12_out, i3);
  not not_13 (not_13_out, i2);
  not not_14 (not_14_out, i5);
  not not_15 (not_15_out, i3);
  not not_16 (not_16_out, i5);
  not not_17 (not_17_out, i4);
  not not_18 (not_18_out, i2);
  not not_19 (not_19_out, i1);
  not not_20 (not_20_out, i0);
  and and_2 (and_2_out, not_1_out, not_2_out, not_3_out, not_4_out, not_5_out, not_6_out);
  and and_3 (and_3_out, i5, not_7_out, i3, not_8_out, i1, not_9_out);
  and and_4 (and_4_out, not_10_out, not_11_out, not_12_out, not_13_out);
  and and_5 (and_5_out, not_14_out, i1);
  and and_6 (and_6_out, not_15_out, i1);
  and and_7 (and_7_out, i2, i0);
  and and_8 (and_8_out, i2, i1);
  and and_9 (and_9_out, i3, i0);
  and and_10 (and_10_out, i4, i0);
  and and_11 (and_11_out, i4, i1);
  and and_12 (jr, not_16_out, not_17_out, i3, not_18_out, not_19_out, not_20_out);
  or or_1 (ALUC2, and_2_out, and_3_out);
  or or_2 (ALUC0, and_4_out, and_5_out, and_6_out, and_7_out, and_8_out, and_9_out, and_10_out, and_11_out);
endmodule

module CU_Opcode_ALU (
  input  o5,
  input  o4,
  input  o3,
  input  o2,
  input  o1,
  input  o0,
  output ALUC2,
  output ALUC1,
  output ALUC0
);

  wire and_2_out, and_3_out, and_4_out, and_5_out, and_6_out, and_7_out, and_8_out, not_1_out, not_2_out,
       not_3_out, not_4_out, not_5_out, not_6_out, not_7_out, not_8_out;

  not not_1 (not_1_out, o5);
  not not_2 (not_2_out, o4);
  not not_3 (not_3_out, o3);
  not not_4 (not_4_out, o1);
  not not_5 (not_5_out, o0);
  not not_6 (not_6_out, o1);
  not not_7 (not_7_out, o5);
  not not_8 (not_8_out, o4);
  and and_1 (ALUC2, not_1_out, not_2_out, o3, o2, o1, o0);
  and and_2 (and_2_out, not_3_out, o2);
  and and_3 (and_3_out, o2, not_4_out);
  and and_4 (and_4_out, o2, not_5_out);
  and and_5 (and_5_out, o4, o2);
  and and_6 (and_6_out, o5, o2);
  and and_7 (and_7_out, not_6_out, o0);
  and and_8 (and_8_out, not_7_out, not_8_out, o3, o2, o0);
  or or_1 (ALUC1, and_2_out, and_3_out, and_4_out, and_5_out, and_6_out);
  or or_2 (ALUC0, and_7_out, and_8_out);
endmodule

module IFU (
  input  in_1,
  input  PCSrc,
  input  [31:0] in_3,
  input  clk,
  input  Reset,
  output [31:0] Instr,
  output [31:0] Instr_2
);

  wire [4:0] multiplexer_2_out, PC_q;
  wire [15:0] adder_2_out, multiplexer_1_out;

  Adder #(.width(16)) adder_1 (.a(16'h1), .b({{11{1'b0}}, PC_q}), .out(Instr_2[15:0]));  // open: cin, cout
  Adder #(.width(16)) adder_2 (.a(Instr_2[15:0]), .b(in_3[15:0]), .out(adder_2_out));  // open: cin, cout
  Multiplexer #(.width(16), .enable("false")) multiplexer_1 (
    .in0(Instr_2[15:0]), .in1(adder_2_out), .out(multiplexer_1_out), .sel(PCSrc));
  Multiplexer #(.width(5), .enable("false")) multiplexer_2 (
    .in0(multiplexer_1_out[4:0]), .in1(in_3[4:0]), .out(multiplexer_2_out), .sel(in_1));
  Register #(.width(5)) PC (.D(multiplexer_2_out), .Q(PC_q), .clk(clk), .clr(Reset));  // open: en
  ROM #(.addrWidth(5), .dataWidth(32)) rom_1 (.addr(PC_q), .data(Instr));  // open: sel

  assign Instr_2[31:16] = {16{1'b0}};
endmodule

module Ext (
  input  Ext_op,
  input  [15:0] in_2,
  output [31:0] out_3
);

  Multiplexer #(.width(32), .enable("false")) multiplexer_1 (
    .in0({{17{in_2[15]}}, in_2[14:0]}), .in1({{16{1'b0}}, in_2}), .out(out_3), .sel(Ext_op));
endmodule

// AND
module Control_op_decode (
  input  _5,
  input  _4,
  input  _3,
  input  _2,
  input  _1,
  input  _0,
  output R,
  output ori,
  output beq,
  output bne,
  output sw,
  output lw,
  output lui,
  output j,
  output jal,
  output sb,
  output lb,
  output addi,
  output addiu
);

  wire not_1_out, not_2_out, not_3_out, not_4_out, not_5_out, not_6_out;

  not not_1 (not_1_out, _5);
  not not_2 (not_2_out, _4);
  not not_3 (not_3_out, _3);
  not not_4 (not_4_out, _1);
  not not_5 (not_5_out, _2);
  not not_6 (not_6_out, _0);
  and u_R (R, not_1_out, not_2_out, not_3_out, not_5_out, not_4_out, not_6_out);
  and u_ori (ori, not_1_out, not_2_out, _3, _2, not_4_out, _0);
  and u_beq (beq, not_1_out, not_2_out, not_3_out, _2, not_4_out, not_6_out);
  and u_bne (bne, not_1_out, not_2_out, not_3_out, _2, not_4_out, _0);
  and u_sw (sw, _5, not_2_out, _3, not_5_out, _1, _0);
  and u_lw (lw, _5, not_2_out, not_3_out, not_5_out, _1, _0);
  and u_lui (lui, not_1_out, not_2_out, _3, _2, _1, _0);
  and u_j (j, not_1_out, not_2_out, not_3_out, not_5_out, _1, not_6_out);
  and u_jal (jal, not_1_out, not_2_out, not_3_out, not_5_out, _1, _0);
  and u_sb (sb, _5, not_2_out, _3, not_5_out, not_4_out, not_6_out);
  and u_lb (lb, _5, not_2_out, not_3_out, not_5_out, not_4_out, not_6_out);
  and u_addi (addi, not_1_out, not_2_out, _3, not_5_out, not_4_out, not_6_out);
  and u_addiu (addiu, not_1_out, not_2_out, _3, not_5_out, not_4_out, _0);
endmodule

// OR
module Control_or_logic (
  input  R,
  input  ori,
  input  beq,
  input  bne,
  input  sw,
  input  lw,
  input  lui,
  input  j,
  input  jal,
  input  sb,
  input  lb,
  input  addi,
  input  addiu,
  input  in_14,
  input  in_15,
  output MemtoReg,
  output MemWrite,
  output Branch,
  output ALUSrc,
  output RegDst,
  output RegWrite,
  output j_Op,
  output luiOp,
  output byte_Op,
  output Ext_Op,
  output bne_2
);

  buf M2R (MemtoReg, lw);  // OR_Gate
  buf MemW (MemWrite, sw);  // OR_Gate
  or u_Branch (Branch, beq, bne);
  or u_ALUSrc (ALUSrc, addiu, ori, sw, lw, lui, addi);
  buf u_RegDst (RegDst, R);  // OR_Gate
  or RegW (RegWrite, jal, addiu, R, ori, lw, lui, addi);
  or u_j_Op (j_Op, j, jal);
  buf lui_Op (luiOp, lui);  // OR_Gate
  or u_byte_Op (byte_Op, sb, lb);
  or u_Ext_Op (Ext_Op, ori, addiu);
  buf u_bne (bne_2, bne);  // OR_Gate
endmodule
