// Logisim project alu.circ as structural Verilog: 3 circuits, main circuit alu
module alu (
  input  [3:0] in_1,
  input  [3:0] in_2,
  input  [1:0] in_3,
  output [3:0] out_4
);

  wire [3:0] adder_1_out, and_1_out, or_1_out, subtractor_1_out;

  Adder #(.width(4)) adder_1 (.a(in_1), .b(in_2), .out(adder_1_out));  // open: cin, cout
  Subtractor #(.width(4)) subtractor_1 (.a(in_1), .b(in_2), .out(subtractor_1_out));  // open: bin, bout
  assign and_1_out = in_1 & in_2;  // AND_Gate and_1, 4 bits wide
  assign or_1_out = in_1 | in_2;  // OR_Gate or_1, 4 bits wide
  Multiplexer #(.select(2), .width(4), .enable("false")) multiplexer_1 (
    .in0(adder_1_out), .in1(subtractor_1_out), .in2(and_1_out), .in3(or_1_out), .out(out_4), .sel(in_3));
endmodule

module circuit (
  input  a,
  input  b,
  input  s,
  output jw,
  output jg
);

  wire and_1_out, and_2_out, and_3_out, and_4_out, and_5_out, and_6_out, and_7_out, not_1_out, not_2_out,
       not_3_out, not_4_out, not_5_out, not_6_out;

  and and_1 (and_1_out, b, s);
  and and_2 (and_2_out, a, s);
  and and_3 (and_3_out, a, b);
  not not_1 (not_1_out, a);
  not not_2 (not_2_out, b);
  not not_3 (not_3_out, a);
  not not_4 (not_4_out, s);
  not not_5 (not_5_out, b);
  not not_6 (not_6_out, s);
  or or_1 (jw, and_1_out, and_2_out, and_3_out);
  and and_4 (and_4_out, not_1_out, not_2_out, s);
  and and_5 (and_5_out, not_3_out, b, not_4_out);
  and and_6 (and_6_out, a, not_5_out, not_6_out);
  and and_7 (and_7_out, a, b, s);
  or or_2 (jg, and_4_out, and_5_out, and_6_out, and_7_out);
endmodule

module _4bit (
  input  [3:0] in_1,
  input  [3:0] in_2,
  output [3:0] out_3
);

  wire part_1_jw, part_2_jw, part_3_jw;

  circuit part_1 (.a(in_1[0]), .b(in_2[0]), .s(1'b0), .jw(part_1_jw), .jg(out_3[0]));
  circuit part_2 (.a(in_1[1]), .b(in_2[1]), .s(part_1_jw), .jw(part_2_jw), .jg(out_3[1]));
  circuit part_3 (.a(in_1[2]), .b(in_2[2]), .s(part_2_jw), .jw(part_3_jw), .jg(out_3[2]));
  circuit part_4 (.a(in_1[3]), .b(in_2[3]), .s(part_3_jw), .jg(out_3[3]));  // open: jw
endmodule
