// Logisim project dzq.circ as structural Verilog
module main (
  input  clr,
  output [31:0] out_2,
  output out_3,
  output [4:0] out_4,
  output [31:0] out_5,
  output out_6,
  output [4:0] out_7,
  output [31:0] out_8
);

  wire ALU_zero, and_1_out, control_1_alusrc, control_1_branch, control_1_jump, control_1_memtoreg,
       control_1_regdst, control_1_regsle, Extender;
  wire [1:0] control_1_alucontrol;
  wire [27:0] ifu_1_pc;
  wire [31:0] adder_1_out, adder_2_out, ALU_out, bit_extender_1_out, bit_extender_2_out, bit_extender_3_out,
       DM_out, grf1_1_out1, ifu_1_pc_2, multiplexer_1_out, multiplexer_2_out, multiplexer_4_out,
       multiplexer_5_out, multiplexer_6_out, shifter_2_out;
  wire [31:28] shifter_1_out;

  Multiplexer #(.width(32), .disabled(0)) multiplexer_1 (
    .in0(adder_1_out), .in1(adder_2_out), .out(multiplexer_1_out), .sel(and_1_out));  // open: en
  // Probe on ifu_1_pc_2
  Multiplexer #(.width(32), .disabled(0)) multiplexer_2 (
    .in0(multiplexer_1_out), .in1(ifu_1_pc_2), .out(multiplexer_2_out), .sel(control_1_jump));  // open: en
  IFU ifu_1 (.new_Pc(multiplexer_2_out), .clr(clr), .out(out_2), .PC({ifu_1_pc_2[31:28], ifu_1_pc}));
  // Probe on out_2[20:16]
  control control_1 (
    .opcode(out_2[31:26]), .func(out_2[5:0]), .MemtoReg(control_1_memtoreg), .MemWrite(out_6),
    .Branch(control_1_branch), .ALUcontrol(control_1_alucontrol), .AluSrc(control_1_alusrc),
    .RegWrite(out_3), .RegDst(control_1_regdst), .RegSle(control_1_regsle), .Extender(Extender),
    .Jump(control_1_jump));
  Multiplexer #(.width(5), .disabled(0)) multiplexer_3 (
    .in0(out_2[20:16]), .in1(out_2[15:11]), .out(out_4), .sel(control_1_regdst));  // open: en
  assign bit_extender_1_out = {{16{out_2[15]}}, out_2[15:0]};  // Bit_Extender bit_extender_1
  assign bit_extender_2_out = {{16{1'b0}}, out_2[15:0]};  // Bit_Extender bit_extender_2
  assign bit_extender_3_out = {{6{1'b0}}, {out_2[20:16], out_2[20:0]}};  // Bit_Extender bit_extender_3
  and and_1 (and_1_out, ALU_zero, control_1_branch);
  GRF1 grf1_1 (
    .data(out_5), .clr(clr), .enable(out_3), .a1(out_2[25:21]), .a3(out_4), .a2(out_2[20:16]),
    .out1(grf1_1_out1), .out2(out_8));
  Multiplexer #(.width(32), .disabled(0)) multiplexer_4 (
    .in0(bit_extender_1_out), .in1(bit_extender_2_out), .out(multiplexer_4_out), .sel(Extender));  // open: en
  Shifter #(.width(32)) shifter_1 (.in(bit_extender_3_out), .\dist (5'b00010), .out({shifter_1_out, ifu_1_pc_2[27:0]}));
  Multiplexer #(.width(32), .disabled(0)) multiplexer_5 (
    .in0(grf1_1_out1), .in1(out_8), .out(multiplexer_5_out), .sel(control_1_regsle));  // open: en
  Multiplexer #(.width(32), .disabled(0)) multiplexer_6 (
    .in0(out_8), .in1(multiplexer_4_out), .out(multiplexer_6_out), .sel(control_1_alusrc));  // open: en
  alu ALU (.sle(control_1_alucontrol), .d1(multiplexer_5_out), .d2(multiplexer_6_out), .zero(ALU_zero), .out(ALU_out));
  Shifter #(.width(32)) shifter_2 (.in(multiplexer_4_out), .\dist (5'b00010), .out(shifter_2_out));
  Adder #(.width(32)) adder_1 (.a({ifu_1_pc_2[31:28], ifu_1_pc}), .b(32'h4), .out(adder_1_out));  // open: cin, cout
  DM DM (.enable(out_6), .address(ALU_out), .\input (out_8), .clr(clr), .addout(out_7), .out(DM_out));
  Adder #(.width(32)) adder_2 (.a(shifter_2_out), .b(adder_1_out), .out(adder_2_out));  // open: cin, cout
  Multiplexer #(.width(32), .disabled(0)) multiplexer_7 (
    .in0(ALU_out), .in1(DM_out), .out(out_5), .sel(control_1_memtoreg));  // open: en

  // Other names for the same wires on the sheet: Instr[31:0] = out_2; MemAddr[4:0] = out_7; MemData[31:0] = out_8;
  //   MemWrite = out_6; RegAddr[4:0] = out_4; RegData[31:0] = out_5; RegWrite = out_3
endmodule

module IFU (
  input  [31:0] new_Pc,
  input  clr,
  output [31:0] out,
  output [31:0] PC
);

  wire clk_out, comparator_1_lt;
  wire [31:0] divider_1_out, rom_1_data;

  Clock clk (.out(clk_out));
  Register #(.width(32)) u_PC (.D(new_Pc), .Q(PC), .clk(clk_out), .clr(clr));  // open: en
  Divider #(.width(32)) divider_1 (.a(PC), .b(32'h4), .out(divider_1_out));  // open: upper, rem
  Comparator #(.width(32), .mode("unsigned")) comparator_1 (
    .a(divider_1_out), .b(32'h20), .lt(comparator_1_lt));  // open: gt, eq
  ROM #(.addrWidth(5), .dataWidth(32)) rom_1 (.addr(divider_1_out[4:0]), .data(rom_1_data));  // open: sel
  Multiplexer #(.width(32), .disabled(0)) multiplexer_1 (
    .in0({32{1'b0}}), .in1(rom_1_data), .out(out), .sel(comparator_1_lt));  // open: en

  // Notes on the sheet:
  //   contents of rom_1 (hex, n*v repeats v):
  //   34040002 348501c8 3c06007b 3c07ffff 34e7ffff 868021 878821 e79021 34080000 ad040000 ad050004
  //   ad060008 ad07000c ad100010 ad110014 ad120018 8d040000 8d050000 ad04001c ad050020 869823 87a023
  //   e7a823 34160001 11040002 1164021 8000018
endmodule

// GRF
module GRF1 (
  input  clr,
  input  [31:0] data,
  input  enable,
  input  [4:0] a1,
  input  [4:0] a2,
  input  [4:0] a3,
  output [31:0] out1,
  output [31:0] out2
);

  wire _0, _1, _2, _3, _4, _5, _6, _7, _8, _9, _10, _11, _12, _13, _14, _15, _16, _17, _18, _19, _20, _21,
       _22, _23, _24, _25, _26, _27, _28, _29, _30, _31, clk;
  wire [31:0] o0, o1, o2, o3, o4, o5, o6, o7, o8, o9, o10, o11, o12, o13, o14, o15, o16, o17, o18, o19, o20,
       o21, o22, o23, o24, o25, o26, o27, o28, o29, o30, o31;

  Decoder #(.select(5), .disabled(0)) decoder_1 (
    .out0(_0), .out1(_1), .out2(_2), .out3(_3), .out4(_4), .out5(_5), .out6(_6), .out7(_7), .out8(_8),
    .out9(_9), .out10(_10), .out11(_11), .out12(_12), .out13(_13), .out14(_14), .out15(_15), .out16(_16),
    .out17(_17), .out18(_18), .out19(_19), .out20(_20), .out21(_21), .out22(_22), .out23(_23), .out24(_24),
    .out25(_25), .out26(_26), .out27(_27), .out28(_28), .out29(_29), .out30(_30), .out31(_31), .sel(a3),
    .en(enable));
  Register #(.width(32)) register_1 (.en(_0), .Q(o0), .clk(clk), .clr(clr));  // open: D
  Register #(.width(32)) register_2 (.D(data), .en(_8), .Q(o8), .clk(clk), .clr(clr));
  Register #(.width(32)) register_3 (.D(data), .en(_16), .Q(o16), .clk(clk), .clr(clr));
  Register #(.width(32)) register_4 (.D(data), .en(_24), .Q(o24), .clk(clk), .clr(clr));
  Register #(.width(32)) register_5 (.D(data), .en(_1), .Q(o1), .clk(clk), .clr(clr));
  Register #(.width(32)) register_6 (.D(data), .en(_9), .Q(o9), .clk(clk), .clr(clr));
  Register #(.width(32)) register_7 (.D(data), .en(_17), .Q(o17), .clk(clk), .clr(clr));
  Register #(.width(32)) register_8 (.D(data), .en(_25), .Q(o25), .clk(clk), .clr(clr));
  Multiplexer #(.select(5), .width(32), .disabled(0)) multiplexer_1 (
    .in0(o0), .in1(o1), .in2(o2), .in3(o3), .in4(o4), .in5(o5), .in6(o6), .in7(o7), .in8(o8), .in9(o9),
    .in10(o10), .in11(o11), .in12(o12), .in13(o13), .in14(o14), .in15(o15), .in16(o16), .in17(o17),
    .in18(o18), .in19(o19), .in20(o20), .in21(o21), .in22(o22), .in23(o23), .in24(o24), .in25(o25),
    .in26(o26), .in27(o27), .in28(o28), .in29(o29), .in30(o30), .in31(o31), .out(out1), .sel(a1));  // open: en
  Register #(.width(32)) register_9 (.D(data), .en(_2), .Q(o2), .clk(clk), .clr(clr));
  Register #(.width(32)) register_10 (.D(data), .en(_10), .Q(o10), .clk(clk), .clr(clr));
  Register #(.width(32)) register_11 (.D(data), .en(_18), .Q(o18), .clk(clk), .clr(clr));
  Register #(.width(32)) register_12 (.D(data), .en(_26), .Q(o26), .clk(clk), .clr(clr));
  Register #(.width(32)) register_13 (.D(data), .en(_3), .Q(o3), .clk(clk), .clr(clr));
  Register #(.width(32)) register_14 (.D(data), .en(_11), .Q(o11), .clk(clk), .clr(clr));
  Register #(.width(32)) register_15 (.D(data), .en(_19), .Q(o19), .clk(clk), .clr(clr));
  Register #(.width(32)) register_16 (.D(data), .en(_27), .Q(o27), .clk(clk), .clr(clr));
  Register #(.width(32)) register_17 (.D(data), .en(_4), .Q(o4), .clk(clk), .clr(clr));
  Register #(.width(32)) register_18 (.D(data), .en(_12), .Q(o12), .clk(clk), .clr(clr));
  Register #(.width(32)) register_19 (.D(data), .en(_20), .Q(o20), .clk(clk), .clr(clr));
  Register #(.width(32)) register_20 (.D(data), .en(_28), .Q(o28), .clk(clk), .clr(clr));
  Multiplexer #(.select(5), .width(32), .disabled(0)) multiplexer_2 (
    .in0(o0), .in1(o1), .in2(o2), .in3(o3), .in4(o4), .in5(o5), .in6(o6), .in7(o7), .in8(o8), .in9(o9),
    .in10(o10), .in11(o11), .in12(o12), .in13(o13), .in14(o14), .in15(o15), .in16(o16), .in17(o17),
    .in18(o18), .in19(o19), .in20(o20), .in21(o21), .in22(o22), .in23(o23), .in24(o24), .in25(o25),
    .in26(o26), .in27(o27), .in28(o28), .in29(o29), .in30(o30), .in31(o31), .out(out2), .sel(a2));  // open: en
  Register #(.width(32)) register_21 (.D(data), .en(_5), .Q(o5), .clk(clk), .clr(clr));
  Register #(.width(32)) register_22 (.D(data), .en(_13), .Q(o13), .clk(clk), .clr(clr));
  Register #(.width(32)) register_23 (.D(data), .en(_21), .Q(o21), .clk(clk), .clr(clr));
  Register #(.width(32)) register_24 (.D(data), .en(_29), .Q(o29), .clk(clk), .clr(clr));
  Register #(.width(32)) register_25 (.D(data), .en(_6), .Q(o6), .clk(clk), .clr(clr));
  Register #(.width(32)) register_26 (.D(data), .en(_14), .Q(o14), .clk(clk), .clr(clr));
  Register #(.width(32)) register_27 (.D(data), .en(_22), .Q(o22), .clk(clk), .clr(clr));
  Register #(.width(32)) register_28 (.D(data), .en(_30), .Q(o30), .clk(clk), .clr(clr));
  Clock clock_1 (.out(clk));
  Register #(.width(32)) register_29 (.D(data), .en(_7), .Q(o7), .clk(clk), .clr(clr));
  Register #(.width(32)) register_30 (.D(data), .en(_15), .Q(o15), .clk(clk), .clr(clr));
  Register #(.width(32)) register_31 (.D(data), .en(_23), .Q(o23), .clk(clk), .clr(clr));
  Register #(.width(32)) register_32 (.D(data), .en(_31), .Q(o31), .clk(clk), .clr(clr));
endmodule

module alu (
  input  [1:0] sle,
  input  [31:0] d1,
  input  [31:0] d2,
  output zero,
  output [31:0] out
);

  wire [31:0] adder_1_out, or_1_out, subtractor_1_out;

  Adder #(.width(32)) adder_1 (.a(d1), .b(d2), .out(adder_1_out));  // open: cin, cout
  Subtractor #(.width(32)) subtractor_1 (.a(d1), .b(d2), .out(subtractor_1_out));  // open: bin, bout
  assign or_1_out = d1 | d2;  // OR_Gate or_1, 32 bits wide
  Multiplexer #(.select(2), .width(32), .disabled(0)) multiplexer_1 (
    .in0(adder_1_out), .in1(subtractor_1_out), .in2(or_1_out), .in3({d2[15:0], {16{1'b0}}}), .out(out),
    .sel(sle));  // open: en
  Comparator #(.width(32), .mode("unsigned")) comparator_1 (
    .a({32{1'b0}}), .b(subtractor_1_out), .eq(zero));  // open: gt, lt
endmodule

module DM (
  input  enable,
  input  [31:0] address,
  input  [31:0] \input ,
  input  clr,
  output [4:0] addout,
  output [31:0] out
);

  wire clock_1_out;
  wire [31:5] divider_1_out;

  Clock clock_1 (.out(clock_1_out));
  Divider #(.width(32)) divider_1 (.a(address), .b(32'h4), .out({divider_1_out, addout}));  // open: upper, rem
  RAM #(.addrWidth(5), .dataWidth(32), .bus("separate")) ram_1 (
    .addr(addout), .din(\input ), .data(out), .str(enable), .clk(clock_1_out), .clr(clr));  // open: sel, ld
endmodule

module control (
  input  [5:0] opcode,
  input  [5:0] func,
  output MemtoReg,
  output MemWrite,
  output Branch,
  output [1:0] ALUcontrol,
  output AluSrc,
  output RegWrite,
  output RegDst,
  output RegSle,
  output Extender,
  output Jump
);

  wire addu, beq, j, lui, lw, nop, not_1_out, not_2_out, not_3_out, not_4_out, not_5_out, not_6_out,
       not_7_out, not_8_out, not_9_out, not_10_out, not_11_out, not_12_out, ori, subu, sw;

  not not_1 (not_1_out, func[5]);
  not not_2 (not_2_out, func[4]);
  not not_3 (not_3_out, func[3]);
  not not_4 (not_4_out, func[2]);
  not not_5 (not_5_out, func[0]);
  not not_6 (not_6_out, func[1]);
  not not_7 (not_7_out, opcode[5]);
  not not_8 (not_8_out, opcode[3]);
  not not_9 (not_9_out, opcode[4]);
  not not_10 (not_10_out, opcode[2]);
  not not_11 (not_11_out, opcode[0]);
  not not_12 (not_12_out, opcode[1]);
  and u_addu (addu, func[5], not_2_out, not_3_out, not_4_out, not_6_out, func[0], not_7_out, not_9_out, not_8_out, not_10_out, not_12_out, not_11_out);
  and u_subu (subu, func[5], not_2_out, not_3_out, not_4_out, func[1], func[0], not_7_out, not_9_out, not_8_out, not_10_out, not_12_out, not_11_out);
  and u_ori (ori, not_7_out, not_9_out, opcode[3], opcode[2], not_12_out, opcode[0]);
  and u_lw (lw, opcode[5], not_9_out, not_8_out, not_10_out, opcode[1], opcode[0]);
  and u_sw (sw, opcode[5], not_9_out, opcode[3], not_10_out, opcode[1], opcode[0]);
  and u_beq (beq, not_7_out, not_9_out, not_8_out, opcode[2], not_12_out, not_11_out);
  and u_lui (lui, not_7_out, not_9_out, opcode[3], opcode[2], opcode[1], opcode[0]);
  and u_nop (nop, not_1_out, not_2_out, not_3_out, not_4_out, not_6_out, not_5_out, not_7_out, not_9_out, not_8_out, not_10_out, not_12_out, not_11_out);
  and lui_2 (j, not_7_out, not_9_out, not_8_out, not_10_out, opcode[1], not_11_out);
  buf or_1 (MemtoReg, lw);  // OR_Gate
  buf or_2 (MemWrite, sw);  // OR_Gate
  buf or_3 (Branch, beq);  // OR_Gate
  or or_4 (ALUcontrol[0], subu, lui, beq);
  or or_5 (ALUcontrol[1], ori, lui);
  or or_6 (AluSrc, ori, lw, sw, lui);
  or or_7 (RegWrite, addu, subu, ori, lw, lui);
  or or_8 (RegDst, addu, subu);
  buf or_9 (RegSle, lui);  // OR_Gate
  or or_10 (Extender, ori, lui);
  buf or_11 (Jump, j);  // OR_Gate
endmodule

module GRF (
  input  enable,
  input  [4:0] a1,
  input  [4:0] a2,
  input  [4:0] a3,
  input  [31:0] d,
  input  clr,
  output [31:0] out_7,
  output [31:0] out_8
);

  wire clock_1_out, decoder_1_out0, decoder_1_out1, decoder_1_out2, decoder_1_out3, decoder_1_out4,
       decoder_1_out5, decoder_1_out6, decoder_1_out7, decoder_1_out8, decoder_1_out9, decoder_1_out10,
       decoder_1_out11, decoder_1_out12, decoder_1_out13, decoder_1_out14, decoder_1_out15, decoder_1_out16,
       decoder_1_out17, decoder_1_out18, decoder_1_out19, decoder_1_out20, decoder_1_out21, decoder_1_out22,
       decoder_1_out23, decoder_1_out24, decoder_1_out25, decoder_1_out26, decoder_1_out27, decoder_1_out28,
       decoder_1_out29, decoder_1_out30, decoder_1_out31;
  wire [31:0] register_1_q, register_2_q, register_3_q, register_4_q, register_5_q, register_6_q,
       register_7_q, register_8_q, register_9_q, register_10_q, register_11_q, register_12_q, register_13_q,
       register_14_q, register_15_q, register_16_q, register_17_q, register_18_q, register_19_q,
       register_20_q, register_21_q, register_22_q, register_23_q, register_24_q, register_25_q,
       register_26_q, register_27_q, register_28_q, register_29_q, register_30_q, register_31_q,
       register_32_q;

  Decoder #(.select(5), .disabled(0)) decoder_1 (
    .out0(decoder_1_out0), .out1(decoder_1_out1), .out2(decoder_1_out2), .out3(decoder_1_out3),
    .out4(decoder_1_out4), .out5(decoder_1_out5), .out6(decoder_1_out6), .out7(decoder_1_out7),
    .out8(decoder_1_out8), .out9(decoder_1_out9), .out10(decoder_1_out10), .out11(decoder_1_out11),
    .out12(decoder_1_out12), .out13(decoder_1_out13), .out14(decoder_1_out14), .out15(decoder_1_out15),
    .out16(decoder_1_out16), .out17(decoder_1_out17), .out18(decoder_1_out18), .out19(decoder_1_out19),
    .out20(decoder_1_out20), .out21(decoder_1_out21), .out22(decoder_1_out22), .out23(decoder_1_out23),
    .out24(decoder_1_out24), .out25(decoder_1_out25), .out26(decoder_1_out26), .out27(decoder_1_out27),
    .out28(decoder_1_out28), .out29(decoder_1_out29), .out30(decoder_1_out30), .out31(decoder_1_out31),
    .sel(a3), .en(enable));
  Clock clock_1 (.out(clock_1_out));
  Register #(.width(32)) register_1 (.en(decoder_1_out0), .Q(register_1_q), .clk(clock_1_out), .clr(clr));  // open: D
  Register #(.width(32)) register_2 (.D(d), .en(decoder_1_out1), .Q(register_2_q), .clk(clock_1_out), .clr(clr));
  Register #(.width(32)) register_3 (.D(d), .en(decoder_1_out2), .Q(register_3_q), .clk(clock_1_out), .clr(clr));
  Register #(.width(32)) register_4 (.D(d), .en(decoder_1_out3), .Q(register_4_q), .clk(clock_1_out), .clr(clr));
  Register #(.width(32)) register_5 (.D(d), .en(decoder_1_out4), .Q(register_5_q), .clk(clock_1_out), .clr(clr));
  Register #(.width(32)) register_6 (.D(d), .en(decoder_1_out5), .Q(register_6_q), .clk(clock_1_out), .clr(clr));
  Register #(.width(32)) register_7 (.D(d), .en(decoder_1_out6), .Q(register_7_q), .clk(clock_1_out), .clr(clr));
  Register #(.width(32)) register_8 (.D(d), .en(decoder_1_out7), .Q(register_8_q), .clk(clock_1_out), .clr(clr));
  Register #(.width(32)) register_9 (.D(d), .en(decoder_1_out8), .Q(register_9_q), .clk(clock_1_out), .clr(clr));
  Register #(.width(32)) register_10 (.D(d), .en(decoder_1_out9), .Q(register_10_q), .clk(clock_1_out), .clr(clr));
  Register #(.width(32)) register_11 (.D(d), .en(decoder_1_out10), .Q(register_11_q), .clk(clock_1_out), .clr(clr));
  Register #(.width(32)) register_12 (.D(d), .en(decoder_1_out11), .Q(register_12_q), .clk(clock_1_out), .clr(clr));
  Register #(.width(32)) register_13 (.D(d), .en(decoder_1_out12), .Q(register_13_q), .clk(clock_1_out), .clr(clr));
  Register #(.width(32)) register_14 (.D(d), .en(decoder_1_out13), .Q(register_14_q), .clk(clock_1_out), .clr(clr));
  Register #(.width(32)) register_15 (.D(d), .en(decoder_1_out14), .Q(register_15_q), .clk(clock_1_out), .clr(clr));
  Register #(.width(32)) register_16 (.D(d), .en(decoder_1_out15), .Q(register_16_q), .clk(clock_1_out), .clr(clr));
  Register #(.width(32)) register_17 (.D(d), .en(decoder_1_out16), .Q(register_17_q), .clk(clock_1_out), .clr(clr));
  Register #(.width(32)) register_18 (.D(d), .en(decoder_1_out17), .Q(register_18_q), .clk(clock_1_out), .clr(clr));
  Register #(.width(32)) register_19 (.D(d), .en(decoder_1_out18), .Q(register_19_q), .clk(clock_1_out), .clr(clr));
  Register #(.width(32)) register_20 (.D(d), .en(decoder_1_out19), .Q(register_20_q), .clk(clock_1_out), .clr(clr));
  Register #(.width(32)) register_21 (.D(d), .en(decoder_1_out20), .Q(register_21_q), .clk(clock_1_out), .clr(clr));
  Register #(.width(32)) register_22 (.D(d), .en(decoder_1_out21), .Q(register_22_q), .clk(clock_1_out), .clr(clr));
  Register #(.width(32)) register_23 (.D(d), .en(decoder_1_out22), .Q(register_23_q), .clk(clock_1_out), .clr(clr));
  Register #(.width(32)) register_24 (.D(d), .en(decoder_1_out23), .Q(register_24_q), .clk(clock_1_out), .clr(clr));
  Register #(.width(32)) register_25 (.D(d), .en(decoder_1_out24), .Q(register_25_q), .clk(clock_1_out), .clr(clr));
  Register #(.width(32)) register_26 (.D(d), .en(decoder_1_out25), .Q(register_26_q), .clk(clock_1_out), .clr(clr));
  Register #(.width(32)) register_27 (.D(d), .en(decoder_1_out26), .Q(register_27_q), .clk(clock_1_out), .clr(clr));
  Register #(.width(32)) register_28 (.D(d), .en(decoder_1_out27), .Q(register_28_q), .clk(clock_1_out), .clr(clr));
  Register #(.width(32)) register_29 (.D(d), .en(decoder_1_out28), .Q(register_29_q), .clk(clock_1_out), .clr(clr));
  Register #(.width(32)) register_30 (.D(d), .en(decoder_1_out29), .Q(register_30_q), .clk(clock_1_out), .clr(clr));
  Register #(.width(32)) register_31 (.D(d), .en(decoder_1_out30), .Q(register_31_q), .clk(clock_1_out), .clr(clr));
  Register #(.width(32)) register_32 (.D(d), .en(decoder_1_out31), .Q(register_32_q), .clk(clock_1_out), .clr(clr));
  Multiplexer #(.select(5), .width(32), .disabled(0)) multiplexer_1 (
    .in0(register_1_q), .in1(register_2_q), .in2(register_3_q), .in3(register_4_q), .in4(register_5_q),
    .in5(register_6_q), .in6(register_7_q), .in7(register_8_q), .in8(register_9_q), .in9(register_10_q),
    .in10(register_11_q), .in11(register_12_q), .in12(register_13_q), .in13(register_14_q),
    .in14(register_15_q), .in15(register_16_q), .in16(register_17_q), .in17(register_18_q),
    .in18(register_19_q), .in19(register_20_q), .in20(register_21_q), .in21(register_22_q),
    .in22(register_23_q), .in23(register_24_q), .in24(register_25_q), .in25(register_26_q),
    .in26(register_27_q), .in27(register_28_q), .in28(register_29_q), .in29(register_30_q),
    .in30(register_31_q), .in31(register_32_q), .out(out_7), .sel(a1));  // open: en
  Multiplexer #(.select(5), .width(32), .disabled(0)) multiplexer_2 (
    .in0(register_1_q), .in1(register_2_q), .in2(register_3_q), .in3(register_4_q), .in4(register_5_q),
    .in5(register_6_q), .in6(register_7_q), .in7(register_8_q), .in8(register_9_q), .in9(register_10_q),
    .in10(register_11_q), .in11(register_12_q), .in12(register_13_q), .in13(register_14_q),
    .in14(register_15_q), .in15(register_16_q), .in16(register_17_q), .in17(register_18_q),
    .in18(register_19_q), .in19(register_20_q), .in20(register_21_q), .in21(register_22_q),
    .in22(register_23_q), .in23(register_24_q), .in24(register_25_q), .in25(register_26_q),
    .in26(register_27_q), .in27(register_28_q), .in28(register_29_q), .in29(register_30_q),
    .in30(register_31_q), .in31(register_32_q), .out(out_8), .sel(a2));  // open: en
endmodule
