// Logisim project fibs.circ as structural Verilog: 8 circuits, main circuit main
module main (
  input  [31:0] in_1,
  output [31:0] out_2
);

  wire clock_1_out, clock_2_out, comparator_1_eq, comparator_2_eq, comparator_3_gt, multiplexer_1_out,
       not_1_out, not_2_out;
  wire [4:0] counter_1_q, register_1_q;
  wire [5:0] counter_2_q, register_2_q;
  wire [31:0] chengfa_1_out_10, chengfa_1_out_11, chengfa_1_out_12, chengfa_1_out_13, multiplexer_2_out,
       multiplexer_3_out, multiplexer_4_out, multiplexer_5_out, multiplexer_6_out, n2bei_1_out_1,
       n2bei_1_out_2, n2bei_1_out_3, n2bei_1_out_4, register_3_q, register_4_q, register_5_q, register_6_q,
       register_7_q, subtractor_1_out;

  Subtractor #(.width(32)) subtractor_1 (.a(in_1), .b(32'h1), .out(subtractor_1_out));  // open: bin, bout
  Counter #(.width(5), .max('h1f)) counter_1 (.Q(counter_1_q), .clk(clock_1_out));  // open: load, D, count, carry, clr
  Comparator #(.width(32), .mode("unsigned")) comparator_1 (
    .a({32{1'b0}}), .b(in_1), .eq(comparator_1_eq));  // open: gt, lt
  Register #(.width(5)) register_1 (.D(counter_1_q), .Q(register_1_q), .clk(clock_1_out));  // open: en, clr
  Clock clock_1 (.out(clock_1_out));
  _2bei u_2bei_1 (.out_1(n2bei_1_out_1), .out_2(n2bei_1_out_2), .out_3(n2bei_1_out_3), .out_4(n2bei_1_out_4));
  Multiplexer #(.select(5)) multiplexer_1 (
    .in0(subtractor_1_out[0]), .in1(subtractor_1_out[1]), .in2(subtractor_1_out[2]),
    .in3(subtractor_1_out[3]), .in4(subtractor_1_out[4]), .in5(subtractor_1_out[5]),
    .in6(subtractor_1_out[6]), .in7(subtractor_1_out[7]), .in8(subtractor_1_out[8]),
    .in9(subtractor_1_out[9]), .in10(subtractor_1_out[10]), .in11(subtractor_1_out[11]),
    .in12(subtractor_1_out[12]), .in13(subtractor_1_out[13]), .in14(subtractor_1_out[14]),
    .in15(subtractor_1_out[15]), .in16(subtractor_1_out[16]), .in17(subtractor_1_out[17]),
    .in18(subtractor_1_out[18]), .in19(subtractor_1_out[19]), .in20(subtractor_1_out[20]),
    .in21(subtractor_1_out[21]), .in22(subtractor_1_out[22]), .in23(subtractor_1_out[23]),
    .in24(subtractor_1_out[24]), .in25(subtractor_1_out[25]), .in26(subtractor_1_out[26]),
    .in27(subtractor_1_out[27]), .in28(subtractor_1_out[28]), .in29(subtractor_1_out[29]),
    .in30(subtractor_1_out[30]), .in31(subtractor_1_out[31]), .out(multiplexer_1_out), .sel(register_1_q));  // open: en
  not not_1 (not_1_out, multiplexer_1_out);
  Multiplexer #(.width(32)) multiplexer_2 (
    .in0(n2bei_1_out_1), .in1(32'h1), .out(multiplexer_2_out), .sel(not_1_out));  // open: en
  Multiplexer #(.width(32)) multiplexer_3 (
    .in0(n2bei_1_out_2), .in1({32{1'b0}}), .out(multiplexer_3_out), .sel(not_1_out));  // open: en
  Multiplexer #(.width(32)) multiplexer_4 (
    .in0(n2bei_1_out_3), .in1({32{1'b0}}), .out(multiplexer_4_out), .sel(not_1_out));  // open: en
  Multiplexer #(.width(32)) multiplexer_5 (
    .in0(n2bei_1_out_4), .in1(32'h1), .out(multiplexer_5_out), .sel(not_1_out));  // open: en
  Register #(.width(6)) register_2 (.D(counter_2_q), .Q(register_2_q), .clk(clock_2_out));  // open: en, clr
  Counter #(.width(6), .max('h20)) counter_2 (.Q(counter_2_q), .clk(clock_2_out));  // open: load, D, count, carry, clr
  Comparator #(.width(6), .mode("unsigned")) comparator_2 (
    .a(counter_2_q), .b(6'b100000), .eq(comparator_2_eq));  // open: gt, lt
  Comparator #(.width(6), .mode("unsigned")) comparator_3 (
    .a(register_2_q), .b(6'b100000), .gt(comparator_3_gt));  // open: eq, lt
  // Probe on chengfa_1_out_10
  // Probe on chengfa_1_out_12
  Register #(.width(32)) register_3 (.D(chengfa_1_out_10), .Q(register_3_q), .clk(clock_2_out));  // open: en, clr
  Register #(.width(32)) register_4 (.D(chengfa_1_out_11), .Q(register_4_q), .clk(clock_2_out));  // open: en, clr
  Register #(.width(32)) register_5 (.D(chengfa_1_out_12), .Q(register_5_q), .clk(clock_2_out));  // open: en, clr
  Register #(.width(32)) register_6 (.D(chengfa_1_out_13), .Q(register_6_q), .clk(clock_2_out));  // open: en, clr
  not not_2 (not_2_out, comparator_3_gt);
  // Probe on chengfa_1_out_11
  // Probe on chengfa_1_out_13
  // Probe on chengfa_1_out_10
  Clock clock_2 (.out(clock_2_out));
  chengfa chengfa_1 (
    .in_1(register_3_q), .in_2(register_4_q), .in_3(register_5_q), .in_4(register_6_q), .in_5(clock_2_out),
    .in_6(multiplexer_2_out), .in_7(multiplexer_3_out), .in_8(multiplexer_4_out), .in_9(multiplexer_5_out),
    .out_10(chengfa_1_out_10), .out_11(chengfa_1_out_11), .out_12(chengfa_1_out_12), .out_13(chengfa_1_out_13));
  Multiplexer #(.width(32)) multiplexer_6 (
    .in0(chengfa_1_out_10), .in1({32{1'b0}}), .out(multiplexer_6_out), .sel(comparator_1_eq));  // open: en
  Register #(.width(32)) register_7 (
    .D(multiplexer_6_out), .en(comparator_2_eq), .Q(register_7_q), .clk(clock_2_out));  // open: clr
  Register #(.width(32)) register_8 (.D(register_7_q), .en(not_2_out), .Q(out_2), .clk(clock_2_out));  // open: clr
endmodule

module op (
  input  [31:0] in_1,
  input  in_2,
  output [31:0] out_3
);

  wire register_1_q, register_2_q;

  Register #(.width(1)) register_1 (.D(register_2_q), .Q(register_1_q), .clk(in_2));  // open: en, clr
  Register #(.width(1)) register_2 (.D(1'b1), .en(1'b1), .Q(register_2_q), .clk(in_2));  // open: clr
  Multiplexer #(.width(32)) multiplexer_1 (.in0(32'h1), .in1(in_1), .out(out_3), .sel(register_1_q));  // open: en
endmodule

module mult (
  input  [31:0] in_1,
  input  [31:0] in_2,
  input  [31:0] in_3,
  input  [31:0] in_4,
  output [31:0] out_5,
  output [31:0] out_6,
  output [31:0] out_7,
  output [31:0] out_8
);

  wire [31:0] multiplier_1_out, multiplier_2_out, multiplier_3_out, multiplier_4_out, multiplier_5_out,
       multiplier_6_out, multiplier_7_out, multiplier_8_out;

  Multiplier #(.width(32)) multiplier_1 (.a(in_1), .b(in_1), .out(multiplier_1_out));  // open: cin, cout
  Multiplier #(.width(32)) multiplier_2 (.a(in_2), .b(in_3), .out(multiplier_2_out));  // open: cin, cout
  Multiplier #(.width(32)) multiplier_3 (.a(in_1), .b(in_2), .out(multiplier_3_out));  // open: cin, cout
  Multiplier #(.width(32)) multiplier_4 (.a(in_2), .b(in_4), .out(multiplier_4_out));  // open: cin, cout
  Multiplier #(.width(32)) multiplier_5 (.a(in_1), .b(in_3), .out(multiplier_5_out));  // open: cin, cout
  Multiplier #(.width(32)) multiplier_6 (.a(in_3), .b(in_4), .out(multiplier_6_out));  // open: cin, cout
  Multiplier #(.width(32)) multiplier_7 (.a(in_2), .b(in_3), .out(multiplier_7_out));  // open: cin, cout
  Multiplier #(.width(32)) multiplier_8 (.a(in_4), .b(in_4), .out(multiplier_8_out));  // open: cin, cout
  Adder #(.width(32)) adder_1 (.a(multiplier_1_out), .b(multiplier_2_out), .out(out_5));  // open: cin, cout
  Adder #(.width(32)) adder_2 (.a(multiplier_3_out), .b(multiplier_4_out), .out(out_6));  // open: cin, cout
  Adder #(.width(32)) adder_3 (.a(multiplier_5_out), .b(multiplier_6_out), .out(out_7));  // open: cin, cout
  Adder #(.width(32)) adder_4 (.a(multiplier_7_out), .b(multiplier_8_out), .out(out_8));  // open: cin, cout
endmodule

module _2bei (
  output [31:0] out_1,
  output [31:0] out_2,
  output [31:0] out_3,
  output [31:0] out_4
);

  wire clock_1_out;
  wire [31:0] mult_1_out_5, mult_1_out_6, mult_1_out_7, mult_1_out_8, register_1_q, register_2_q,
       register_3_q, register_4_q;

  // Probe on out_1
  Register #(.width(32)) register_1 (.D(out_1), .Q(register_1_q), .clk(clock_1_out));  // open: en, clr
  Register #(.width(32)) register_2 (.D(out_2), .Q(register_2_q), .clk(clock_1_out));  // open: en, clr
  Register #(.width(32)) register_3 (.D(out_3), .Q(register_3_q), .clk(clock_1_out));  // open: en, clr
  Register #(.width(32)) register_4 (.D(out_4), .Q(register_4_q), .clk(clock_1_out));  // open: en, clr
  Clock clock_1 (.out(clock_1_out));
  // Probe on out_1
  mult mult_1 (
    .in_1(register_1_q), .in_2(register_2_q), .in_3(register_3_q), .in_4(register_4_q), .out_5(mult_1_out_5),
    .out_6(mult_1_out_6), .out_7(mult_1_out_7), .out_8(mult_1_out_8));
  op op_1 (.in_1(mult_1_out_5), .in_2(clock_1_out), .out_3(out_1));
  op op_2 (.in_1(mult_1_out_6), .in_2(clock_1_out), .out_3(out_2));
  op op_3 (.in_1(mult_1_out_7), .in_2(clock_1_out), .out_3(out_3));
  op3 op3_1 (.in_1(mult_1_out_8), .in_2(clock_1_out), .out_3(out_4));
endmodule

module op3 (
  input  [31:0] in_1,
  input  in_2,
  output [31:0] out_3
);

  wire register_1_q, register_2_q;

  Register #(.width(1)) register_1 (.D(register_2_q), .Q(register_1_q), .clk(in_2));  // open: en, clr
  Register #(.width(1)) register_2 (.D(1'b1), .en(1'b1), .Q(register_2_q), .clk(in_2));  // open: clr
  Multiplexer #(.width(32)) multiplexer_1 (.in0({32{1'b0}}), .in1(in_1), .out(out_3), .sel(register_1_q));  // open: en
endmodule

module chengfa (
  input  [31:0] in_1,
  input  [31:0] in_2,
  input  [31:0] in_3,
  input  [31:0] in_4,
  input  in_5,
  input  [31:0] in_6,
  input  [31:0] in_7,
  input  [31:0] in_8,
  input  [31:0] in_9,
  output [31:0] out_10,
  output [31:0] out_11,
  output [31:0] out_12,
  output [31:0] out_13
);

  wire [31:0] adder_1_out, adder_2_out, adder_3_out, adder_4_out, multiplier_1_out, multiplier_2_out,
       multiplier_3_out, multiplier_4_out, multiplier_5_out, multiplier_6_out, multiplier_7_out,
       multiplier_8_out;

  Multiplier #(.width(32)) multiplier_1 (.a(in_1), .b(in_6), .out(multiplier_1_out));  // open: cin, cout
  Multiplier #(.width(32)) multiplier_2 (.a(in_2), .b(in_8), .out(multiplier_2_out));  // open: cin, cout
  Multiplier #(.width(32)) multiplier_3 (.a(in_1), .b(in_7), .out(multiplier_3_out));  // open: cin, cout
  Multiplier #(.width(32)) multiplier_4 (.a(in_2), .b(in_9), .out(multiplier_4_out));  // open: cin, cout
  Multiplier #(.width(32)) multiplier_5 (.a(in_1), .b(in_8), .out(multiplier_5_out));  // open: cin, cout
  Multiplier #(.width(32)) multiplier_6 (.a(in_3), .b(in_9), .out(multiplier_6_out));  // open: cin, cout
  Multiplier #(.width(32)) multiplier_7 (.a(in_2), .b(in_8), .out(multiplier_7_out));  // open: cin, cout
  Multiplier #(.width(32)) multiplier_8 (.a(in_4), .b(in_9), .out(multiplier_8_out));  // open: cin, cout
  Adder #(.width(32)) adder_1 (.a(multiplier_1_out), .b(multiplier_2_out), .out(adder_1_out));  // open: cin, cout
  Adder #(.width(32)) adder_2 (.a(multiplier_3_out), .b(multiplier_4_out), .out(adder_2_out));  // open: cin, cout
  Adder #(.width(32)) adder_3 (.a(multiplier_5_out), .b(multiplier_6_out), .out(adder_3_out));  // open: cin, cout
  Adder #(.width(32)) adder_4 (.a(multiplier_7_out), .b(multiplier_8_out), .out(adder_4_out));  // open: cin, cout
  _3bei u_3bei_1 (.in_1(adder_1_out), .in_2(in_5), .out_3(out_10));
  _4bei u_4bei_1 (.in_1(adder_2_out), .in_2(in_5), .out_3(out_11));
  _4bei u_4bei_2 (.in_1(adder_3_out), .in_2(in_5), .out_3(out_12));
  _3bei u_3bei_2 (.in_1(adder_4_out), .in_2(in_5), .out_3(out_13));
endmodule

module _3bei (
  input  [31:0] in_1,
  input  in_2,
  output [31:0] out_3
);

  wire register_1_q;

  Register #(.width(1)) register_1 (.D(1'b1), .en(1'b1), .Q(register_1_q), .clk(in_2));  // open: clr
  Multiplexer #(.width(32)) multiplexer_1 (.in0(32'h1), .in1(in_1), .out(out_3), .sel(register_1_q));  // open: en
endmodule

module _4bei (
  input  [31:0] in_1,
  input  in_2,
  output [31:0] out_3
);

  wire register_1_q;

  Register #(.width(1)) register_1 (.D(1'b1), .en(1'b1), .Q(register_1_q), .clk(in_2));  // open: clr
  Multiplexer #(.width(32)) multiplexer_1 (.in0({32{1'b0}}), .in1(in_1), .out(out_3), .sel(register_1_q));  // open: en
endmodule
