// Logisim project fsm.circ as structural Verilog: 1 circuit, main circuit fsm
module fsm (
  input  in_1,
  input  [1:0] in_2,
  output out_3
);

  wire and_1_out, and_2_out, and_3_out, and_4_out, and_5_out, and_6_out, and_7_out, and_8_out, and_9_out,
       and_10_out, and_11_out, and_12_out, and_13_out, and_14_out, and_15_out, clock_1_out,
       multiplexer_1_out, multiplexer_2_out, multiplexer_3_out, not_1_out, not_2_out, not_3_out, not_4_out,
       not_5_out, not_6_out, not_7_out, not_8_out, not_9_out, not_10_out, not_11_out, not_12_out, not_13_out,
       not_14_out, not_15_out, not_16_out, not_17_out, not_18_out, not_19_out, not_20_out, not_21_out,
       not_22_out, not_23_out, not_24_out, not_25_out, not_26_out, not_27_out, not_28_out, not_29_out,
       not_30_out, not_31_out, not_32_out, not_33_out, not_34_out, not_35_out, not_36_out, not_37_out,
       not_38_out, not_39_out, not_40_out, not_41_out, not_42_out, not_43_out, not_44_out, not_45_out,
       not_46_out, not_47_out, not_48_out, not_49_out, not_50_out, or_1_out, or_2_out, or_3_out,
       register_1_q, register_2_q, register_3_q;

  not not_1 (not_1_out, in_2[0]);
  not not_2 (not_2_out, in_2[1]);
  not not_3 (not_3_out, register_2_q);
  not not_4 (not_4_out, register_3_q);
  not not_5 (not_5_out, in_2[0]);
  not not_6 (not_6_out, in_2[1]);
  not not_7 (not_7_out, register_1_q);
  not not_8 (not_8_out, register_3_q);
  not not_9 (not_9_out, in_2[1]);
  not not_10 (not_10_out, register_1_q);
  not not_11 (not_11_out, register_2_q);
  not not_12 (not_12_out, register_3_q);
  not not_13 (not_13_out, in_2[1]);
  not not_14 (not_14_out, register_3_q);
  not not_15 (not_15_out, in_2[1]);
  not not_16 (not_16_out, register_1_q);
  not not_17 (not_17_out, register_2_q);
  not not_18 (not_18_out, in_2[0]);
  not not_19 (not_19_out, register_2_q);
  not not_20 (not_20_out, register_3_q);
  not not_21 (not_21_out, in_2[0]);
  not not_22 (not_22_out, register_1_q);
  not not_23 (not_23_out, register_3_q);
  not not_24 (not_24_out, in_2[0]);
  not not_25 (not_25_out, in_2[1]);
  not not_26 (not_26_out, register_2_q);
  not not_27 (not_27_out, register_3_q);
  not not_28 (not_28_out, in_2[0]);
  not not_29 (not_29_out, in_2[1]);
  not not_30 (not_30_out, register_1_q);
  not not_31 (not_31_out, register_3_q);
  not not_32 (not_32_out, in_2[1]);
  not not_33 (not_33_out, register_2_q);
  not not_34 (not_34_out, register_3_q);
  not not_35 (not_35_out, in_2[1]);
  not not_36 (not_36_out, register_1_q);
  not not_37 (not_37_out, register_3_q);
  not not_38 (not_38_out, in_2[0]);
  not not_39 (not_39_out, register_2_q);
  not not_40 (not_40_out, register_3_q);
  not not_41 (not_41_out, in_2[0]);
  not not_42 (not_42_out, register_1_q);
  not not_43 (not_43_out, register_3_q);
  not not_44 (not_44_out, in_2[0]);
  not not_45 (not_45_out, in_2[1]);
  not not_46 (not_46_out, register_3_q);
  not not_47 (not_47_out, in_2[0]);
  not not_48 (not_48_out, register_3_q);
  and and_1 (and_1_out, not_1_out, not_2_out, register_1_q, not_3_out, not_4_out);
  and and_2 (and_2_out, not_5_out, not_6_out, not_7_out, register_2_q, not_8_out);
  and and_3 (and_3_out, in_2[0], not_9_out, not_10_out, not_11_out, not_12_out);
  and and_4 (and_4_out, in_2[0], not_13_out, register_1_q, register_2_q, not_14_out);
  and and_5 (and_5_out, in_2[0], not_15_out, not_16_out, not_17_out, register_3_q);
  and and_6 (and_6_out, not_18_out, in_2[1], register_1_q, not_19_out, not_20_out);
  and and_7 (and_7_out, not_21_out, in_2[1], not_22_out, register_2_q, not_23_out);
  and and_8 (and_8_out, not_24_out, not_25_out, register_1_q, not_26_out, not_27_out);
  and and_9 (and_9_out, not_28_out, not_29_out, not_30_out, register_2_q, not_31_out);
  and and_10 (and_10_out, in_2[0], not_32_out, register_1_q, not_33_out, not_34_out);
  and and_11 (and_11_out, in_2[0], not_35_out, not_36_out, register_2_q, not_37_out);
  and and_12 (and_12_out, not_38_out, in_2[1], register_1_q, not_39_out, not_40_out);
  and and_13 (and_13_out, not_41_out, in_2[1], not_42_out, register_2_q, not_43_out);
  and and_14 (and_14_out, not_44_out, not_45_out, register_1_q, register_2_q, not_46_out);
  and and_15 (and_15_out, not_47_out, in_2[1], register_1_q, register_2_q, not_48_out);
  or or_1 (or_1_out, and_1_out, and_2_out, and_3_out, and_4_out, and_5_out, and_6_out, and_7_out);
  or or_2 (or_2_out, and_8_out, and_9_out, and_10_out, and_11_out, and_12_out, and_13_out);
  or or_3 (or_3_out, and_14_out, and_15_out);
  Multiplexer multiplexer_1 (.in0(or_1_out), .in1(1'b0), .out(multiplexer_1_out), .sel(in_1));  // open: en
  Multiplexer multiplexer_2 (.in0(or_2_out), .in1(1'b0), .out(multiplexer_2_out), .sel(in_1));  // open: en
  Multiplexer multiplexer_3 (.in0(or_3_out), .in1(1'b0), .out(multiplexer_3_out), .sel(in_1));  // open: en
  Clock clock_1 (.out(clock_1_out));
  Register #(.width(1)) register_1 (.D(multiplexer_1_out), .Q(register_1_q), .clk(clock_1_out));  // open: en, clr
  Register #(.width(1)) register_2 (.D(multiplexer_2_out), .Q(register_2_q), .clk(clock_1_out));  // open: en, clr
  Register #(.width(1)) register_3 (.D(multiplexer_3_out), .Q(register_3_q), .clk(clock_1_out));  // open: en, clr
  not not_49 (not_49_out, or_1_out);
  not not_50 (not_50_out, or_2_out);
  and and_16 (out_3, not_49_out, not_50_out, or_3_out);
endmodule
