// Logisim project mod5.circ as structural Verilog: 4 circuits, main circuit mod5
module mod5 (
  input  in_1,
  output _0,
  output _1,
  output _2,
  output _3,
  output _4
);

  wire and_1_out, and_2_out, and_3_out, and_4_out, and_5_out, and_6_out, and_7_out, and_8_out, and_9_out,
       and_10_out, and_11_out, and_12_out, clock_1_out, not_1_out, not_2_out, not_3_out, not_4_out,
       not_5_out, not_6_out, not_7_out, not_8_out, not_9_out, not_10_out, not_11_out, not_12_out, not_13_out,
       not_14_out, not_15_out, not_16_out, not_17_out, or_1_out, or_2_out, register_1_q, register_2_q;
  wire [2:0] or_3_out;

  not not_1 (not_1_out, in_1);
  not not_2 (not_2_out, register_1_q);
  not not_3 (not_3_out, register_1_q);
  not not_4 (not_4_out, register_2_q);
  not not_5 (not_5_out, in_1);
  not not_6 (not_6_out, register_2_q);
  not not_7 (not_7_out, register_1_q);
  not not_8 (not_8_out, register_2_q);
  not not_9 (not_9_out, in_1);
  not not_10 (not_10_out, register_1_q);
  not not_11 (not_11_out, in_1);
  not not_12 (not_12_out, register_2_q);
  and and_1 (and_1_out, not_1_out, not_2_out, register_2_q);
  and and_2 (and_2_out, in_1, not_3_out, register_2_q);
  and and_3 (and_3_out, in_1, register_1_q, not_4_out);
  and and_4 (and_4_out, not_5_out, register_1_q, not_6_out);
  and and_5 (and_5_out, in_1, not_7_out, not_8_out);
  and and_6 (and_6_out, not_9_out, not_10_out, register_2_q);
  and and_7 (and_7_out, not_11_out, register_1_q, not_12_out);
  and and_8 (and_8_out, in_1, register_1_q, register_2_q);
  or or_1 (or_1_out, and_1_out, and_2_out, and_3_out, and_4_out);
  or or_2 (or_2_out, and_5_out, and_6_out, and_7_out, and_8_out);
  Clock clock_1 (.out(clock_1_out));
  Register #(.width(1)) register_1 (.D(or_1_out), .Q(register_1_q), .clk(clock_1_out));  // open: en, clr
  // Probe on or_1_out
  // Probe on or_2_out
  Register #(.width(1)) register_2 (.D(or_2_out), .Q(register_2_q), .clk(clock_1_out));  // open: en, clr
  not not_13 (not_13_out, or_1_out);
  not not_14 (not_14_out, or_2_out);
  not not_15 (not_15_out, or_2_out);
  not not_16 (not_16_out, or_1_out);
  not not_17 (not_17_out, or_2_out);
  and and_9 (and_9_out, not_13_out, not_14_out, 1'b1);
  or or_3 (or_3_out[0], and_9_out, and_10_out);
  and and_10 (and_10_out, or_1_out, not_15_out, 1'b1);
  and and_11 (and_11_out, not_16_out, or_2_out, 1'b1);
  or or_4 (or_3_out[1], and_11_out, and_12_out);
  and and_12 (and_12_out, or_1_out, not_17_out, 1'b1);
  and and_13 (or_3_out[2], or_1_out, or_2_out, 1'b1);
  // Probe on or_3_out
  Decoder #(.select(3), .enable("false")) decoder_1 (
    .out0(_0), .out1(_1), .out2(_2), .out3(_3), .out4(_4), .sel(or_3_out));  // open: out5, out6, out7
endmodule

module _1 (
  input  in_1,
  input  D,
  output out_3,
  output out_4
);

  wire and_1_out, and_2_out, not_1_out, or_1_out, or_2_out;

  not not_1 (not_1_out, D);
  and and_1 (and_1_out, in_1, D);
  and and_2 (and_2_out, in_1, not_1_out);
  or or_1 (or_1_out, and_1_out, out_4);
  or or_2 (or_2_out, out_3, and_2_out);
  not not_2 (out_3, or_1_out);
  not not_3 (out_4, or_2_out);
endmodule

module _2 (
  input  in_1,
  output out_2
);

  wire clock_1_out, n1_1_out_3, not_1_out;

  not not_1 (not_1_out, clock_1_out);
  _1 u_1_1 (.in_1(not_1_out), .D(in_1), .out_3(n1_1_out_3));  // open: out_4
  Clock clock_1 (.out(clock_1_out));
  _1 u_1_2 (.in_1(clock_1_out), .D(n1_1_out_3), .out_3(out_2));  // open: out_4
endmodule

module test (
  output out_1,
  output out_2,
  output out_3,
  output out_4,
  output out_5,
  output out_6
);

  wire clock_1_out;

  Clock clock_1 (.out(clock_1_out));
  Register register_1 (.clk(clock_1_out));  // open: D, en, Q, clr
  RAM #(.dataWidth(1)) ram_1 (.data(out_1));  // open: addr, sel, clk, ld, clr
  mod5 mod5_1 (.in_1(out_1), ._0(out_2), ._1(out_3), ._2(out_4), ._3(out_5), ._4(out_6));
endmodule
