// Logisim project swap.circ as structural Verilog: 2 circuits, main circuit main
module main (
);

  swap swap_1 ();  // open: in_1, in_2, in_3, out_4, out_5
endmodule

module swap (
  input  in_1,
  input  in_2,
  input  in_3,
  output out_4,
  output out_5
);

  wire not_1_out;

  assign out_4 = not_1_out ? in_1 : 1'bz;  // Controlled_Buffer controlled_buffer_1
  not not_1 (not_1_out, in_3);
  assign out_5 = in_3 ? in_1 : 1'bz;  // Controlled_Buffer controlled_buffer_2
  assign out_5 = not_1_out ? in_2 : 1'bz;  // Controlled_Buffer controlled_buffer_3
  assign out_4 = in_3 ? in_2 : 1'bz;  // Controlled_Buffer controlled_buffer_4
endmodule
