// Logisim project 作业test.circ as structural Verilog: 1 circuit, main circuit main
module main (
  input  a,
  input  b,
  input  c,
  input  d,
  output y,
  output z
);

  wire and_1_out, and_2_out, and_3_out, and_4_out, and_5_out, not_1_out, not_2_out, not_3_out, not_4_out;

  not not_1 (not_1_out, a);
  not not_2 (not_2_out, b);
  not not_3 (not_3_out, c);
  not not_4 (not_4_out, d);
  and and_1 (and_1_out, not_1_out, d);
  and and_2 (and_2_out, b, d);
  and and_3 (and_3_out, a, not_3_out, d);
  and and_4 (and_4_out, a, not_2_out, c);
  and and_5 (and_5_out, a, b, c, d);
  or or_1 (y, and_1_out, and_3_out, and_4_out, and_5_out);
  or or_2 (z, and_2_out, and_3_out);
endmodule
