// Logisim project 加法器.circ as structural Verilog: 4 circuits, main circuit main
module main (
  input  in_1,
  input  in_2,
  input  in_3,
  input  in_4,
  input  in_5,
  input  in_6,
  input  in_7,
  input  in_8,
  input  in_9,
  output out_10,
  output out_11,
  output out_12,
  output out_13
);

  wire \一个加法器_1_out_5 , \一个加法器_2_out_5 , \一个加法器_3_out_5 ;

  \一个加法器  \u_一个加法器_1  (.in_1(in_1), .in_2(in_6), .in_3(in_5), .out_4(out_10), .out_5(\一个加法器_1_out_5 ));
  \一个加法器  \u_一个加法器_2  (.in_1(in_2), .in_2(in_7), .in_3(\一个加法器_1_out_5 ), .out_4(out_11), .out_5(\一个加法器_2_out_5 ));
  \一个加法器  \u_一个加法器_3  (.in_1(in_3), .in_2(in_8), .in_3(\一个加法器_2_out_5 ), .out_4(out_12), .out_5(\一个加法器_3_out_5 ));
  \一个加法器  \u_一个加法器_4  (.in_1(in_4), .in_2(in_9), .in_3(\一个加法器_3_out_5 ), .out_4(out_13));  // open: out_5
endmodule

module c (
  input  in_1,
  input  in_2,
  input  in_3,
  output out_4
);

  wire and_1_out, and_2_out, and_3_out;

  and and_1 (and_1_out, in_1, in_2);
  and and_2 (and_2_out, in_2, in_3);
  and and_3 (and_3_out, in_1, in_3);
  or or_1 (out_4, and_1_out, and_3_out, and_2_out);
endmodule

module s (
  input  in_1,
  input  in_2,
  input  in_3,
  output out_4
);

  wire and_1_out, and_2_out, and_3_out, and_4_out, not_1_out, not_2_out, not_3_out, not_4_out, not_5_out,
       not_6_out;

  not not_1 (not_1_out, in_1);
  not not_2 (not_2_out, in_2);
  not not_3 (not_3_out, in_1);
  not not_4 (not_4_out, in_3);
  not not_5 (not_5_out, in_2);
  not not_6 (not_6_out, in_3);
  and and_1 (and_1_out, not_1_out, not_2_out, in_3);
  and and_2 (and_2_out, not_3_out, in_2, not_4_out);
  and and_3 (and_3_out, in_1, not_5_out, not_6_out);
  and and_4 (and_4_out, in_1, in_2, in_3);
  or or_1 (out_4, and_1_out, and_2_out, and_3_out, and_4_out);
endmodule

module \一个加法器  (
  input  in_1,
  input  in_2,
  input  in_3,
  output out_4,
  output out_5
);

  s s_1 (.in_1(in_1), .in_2(in_2), .in_3(in_3), .out_4(out_4));
  c c_1 (.in_1(in_1), .in_2(in_2), .in_3(in_3), .out_4(out_5));
endmodule
